// Logisim project JKFlipFlop.circ as structural Verilog: 1 circuit, main circuit main
module main (
  input  J,
  input  K,
  output Q,
  output Q_prime
);

  wire and_1_out, and_2_out, and_3_out, and_4_out, CLK_out, nand_1_out, nand_2_out, nor_1_out, nor_2_out,
       not_1_out;

  Clock CLK (.out(CLK_out));
  nand nand_1 (nand_1_out, Q, K);
  nand nand_2 (nand_2_out, J, Q_prime);
  and and_1 (and_1_out, nand_1_out, J, not_1_out);
  and and_2 (and_2_out, K, not_1_out, nand_2_out);
  not not_1 (not_1_out, CLK_out);
  nor nor_1 (nor_1_out, and_1_out, nor_2_out);
  nor nor_2 (nor_2_out, nor_1_out, and_2_out);
  and and_3 (and_3_out, CLK_out, nor_1_out);
  and and_4 (and_4_out, nor_2_out, CLK_out);
  nor nor_3 (Q, and_3_out, Q_prime);
  nor nor_4 (Q_prime, Q, and_4_out);

  // Notes on the sheet:
  //   Clocked JK Flip Flop
  //   Change state on PGT of CLK
endmodule
