// Logisim project adder.circ as structural Verilog: 4 circuits, main circuit add
module add (
  input  a,
  input  b,
  output s,
  output c
);

  wire not_1_out, not_2_out, or_1_out, or_2_out;

  not not_1 (not_1_out, a);
  not not_2 (not_2_out, b);
  and and_1 (c, a, b);
  or or_1 (or_1_out, a, b);
  or or_2 (or_2_out, not_1_out, not_2_out);
  and and_2 (s, or_1_out, or_2_out);
endmodule

// FA
module fa (
  input  A,
  input  B,
  input  Cin,
  output S,
  output Cout
);

  wire add_1_c, add_1_s, add_2_c;

  add add_1 (.a(A), .b(B), .s(add_1_s), .c(add_1_c));
  add add_2 (.a(add_1_s), .b(Cin), .s(S), .c(add_2_c));
  or or_1 (Cout, add_2_c, add_1_c);
endmodule

module _4bit_adder (
  input  Cin,
  input  a0,
  input  a1,
  input  a2,
  input  a3,
  input  b0,
  input  b1,
  input  b2,
  input  b3,
  output s0,
  output s1,
  output s2,
  output s3,
  output Cout
);

  wire fa_1_cout, fa_2_cout, fa_3_cout;

  fa fa_1 (.A(a0), .B(b0), .Cin(Cin), .S(s0), .Cout(fa_1_cout));
  fa fa_2 (.A(a1), .B(b1), .Cin(fa_1_cout), .S(s1), .Cout(fa_2_cout));
  fa fa_3 (.A(a2), .B(b2), .Cin(fa_2_cout), .S(s2), .Cout(fa_3_cout));
  fa fa_4 (.A(a3), .B(b3), .Cin(fa_3_cout), .S(s3), .Cout(Cout));
endmodule

module _8bit_adder (
  input  in_1,
  input  [7:0] in_2,
  input  [7:0] in_3,
  output [7:0] out_4,
  output out_5
);

  wire n4bit_adder_1_cout;

  _4bit_adder u_4bit_adder_1 (
    .a0(in_2[0]), .a1(in_2[1]), .a2(in_2[2]), .a3(in_2[3]), .b0(in_3[0]), .b1(in_3[1]), .b2(in_3[2]),
    .b3(in_3[3]), .Cin(in_1), .Cout(n4bit_adder_1_cout), .s0(out_4[0]), .s1(out_4[1]), .s2(out_4[2]),
    .s3(out_4[3]));
  _4bit_adder u_4bit_adder_2 (
    .a0(in_2[4]), .a1(in_2[5]), .a2(in_2[6]), .a3(in_2[7]), .b0(in_3[4]), .b1(in_3[5]), .b2(in_3[6]),
    .b3(in_3[7]), .Cin(n4bit_adder_1_cout), .Cout(out_5), .s0(out_4[4]), .s1(out_4[5]), .s2(out_4[6]),
    .s3(out_4[7]));
endmodule
