// Logisim project cpu-2020.circ as structural Verilog
module _2x1_mux (
  input  S,
  input  I0,
  input  I1,
  output O
);

  wire and_1_out, and_2_out, not_1_out;

  not not_1 (not_1_out, S);
  and and_1 (and_1_out, not_1_out, I0);
  and and_2 (and_2_out, S, I1);
  or or_1 (O, and_1_out, and_2_out);
endmodule

module _4x1_mux (
  input  S1,
  input  S0,
  input  I0,
  input  I1,
  input  I2,
  input  I3,
  output out_7
);

  wire and_1_out, and_2_out, and_3_out, and_4_out, not_1_out, not_2_out;

  not not_1 (not_1_out, S1);
  not not_2 (not_2_out, S0);
  and and_1 (and_1_out, not_2_out, not_1_out, I0);
  and and_2 (and_2_out, S0, not_1_out, I1);
  and and_3 (and_3_out, not_2_out, S1, I2);
  and and_4 (and_4_out, S0, S1, I3);
  or or_1 (out_7, and_1_out, and_2_out, and_3_out, and_4_out);
endmodule

// 1 LU
module _1bit_LU (
  input  A,
  input  B,
  input  S1,
  input  S0,
  output out_5
);

  wire and_1_out, not_1_out, or_1_out, xor_1_out;

  and and_1 (and_1_out, A, B);
  or or_1 (or_1_out, A, B);
  xor xor_1 (xor_1_out, A, B);
  not not_1 (not_1_out, A);
  _4x1_mux u_4x1_mux_1 (.S1(S1), .S0(S0), .I0(and_1_out), .I1(or_1_out), .I2(xor_1_out), .I3(not_1_out), .out_7(out_5));
endmodule

// 4 LU
module _4bit_LU (
  input  [3:0] A,
  input  [3:0] B,
  input  S1,
  input  S0,
  output [3:0] F
);

  _1bit_LU u_1bit_lu_1 (.A(A[0]), .B(B[0]), .S1(S1), .S0(S0), .out_5(F[0]));
  _1bit_LU u_1bit_lu_2 (.A(A[1]), .B(B[1]), .S1(S1), .S0(S0), .out_5(F[1]));
  _1bit_LU u_1bit_lu_3 (.A(A[2]), .B(B[2]), .S1(S1), .S0(S0), .out_5(F[2]));
  _1bit_LU u_1bit_lu_4 (.A(A[3]), .B(B[3]), .S1(S1), .S0(S0), .out_5(F[3]));
endmodule

// 8 LU
module _8bit_LU (
  input  [7:0] A,
  input  [7:0] B,
  input  S1,
  input  S0,
  output [7:0] F
);

  _4bit_LU u_4bit_lu_1 (.A(A[3:0]), .B(B[3:0]), .S1(S1), .S0(S0), .F(F[3:0]));
  _4bit_LU u_4bit_lu_2 (.A(A[7:4]), .B(B[7:4]), .S1(S1), .S0(S0), .F(F[7:4]));
endmodule

// 4 SH
module _4bit_shifter (
  input  SLin,
  input  [3:0] I,
  input  SRin,
  input  S1,
  input  S0,
  output [3:0] out_6
);

  _4x1_mux u_4x1_mux_1 (.S1(S1), .S0(S0), .I0(I[0]), .I1(SLin), .I2(I[1]), .out_7(out_6[0]));  // open: I3
  _4x1_mux u_4x1_mux_2 (.S1(S1), .S0(S0), .I0(I[1]), .I1(I[0]), .I2(I[2]), .out_7(out_6[1]));  // open: I3
  _4x1_mux u_4x1_mux_3 (.S1(S1), .S0(S0), .I0(I[2]), .I1(I[1]), .I2(I[3]), .out_7(out_6[2]));  // open: I3
  _4x1_mux u_4x1_mux_4 (.S1(S1), .S0(S0), .I0(I[3]), .I1(I[2]), .I2(SRin), .out_7(out_6[3]));  // open: I3
endmodule

// 8 SH
module _8bit_shifter (
  input  SLin,
  input  [7:0] I,
  input  SRin,
  input  S1,
  input  S0,
  output [7:0] O
);

  _4bit_shifter u_4bit_shifter_1 (.I(I[3:0]), .S1(S1), .S0(S0), .SLin(SLin), .SRin(I[4]), .out_6(O[3:0]));
  _4bit_shifter u_4bit_shifter_2 (.I(I[7:4]), .S1(S1), .S0(S0), .SLin(I[3]), .SRin(SRin), .out_6(O[7:4]));
endmodule

// FA
module full_adder (
  input  A,
  input  B,
  input  Cin,
  output S,
  output Cout
);

  wire and_1_out, and_2_out, and_3_out, and_4_out, and_5_out, and_6_out, and_7_out, not_1_out, not_2_out,
       not_3_out, not_4_out, not_5_out, not_6_out;

  not not_1 (not_1_out, A);
  not not_2 (not_2_out, B);
  not not_3 (not_3_out, A);
  not not_4 (not_4_out, Cin);
  not not_5 (not_5_out, B);
  not not_6 (not_6_out, Cin);
  and and_1 (and_1_out, B, Cin);
  and and_2 (and_2_out, A, Cin);
  and and_3 (and_3_out, A, B);
  and and_4 (and_4_out, not_1_out, not_2_out, Cin);
  and and_5 (and_5_out, not_3_out, B, not_4_out);
  and and_6 (and_6_out, A, not_5_out, not_6_out);
  and and_7 (and_7_out, A, B, Cin);
  or or_1 (Cout, and_1_out, and_2_out, and_3_out);
  or or_2 (S, and_4_out, and_5_out, and_6_out, and_7_out);
endmodule

// 1 AU
module _1bit_AU (
  input  Ci,
  input  A,
  input  B,
  input  S1,
  input  S0,
  output F,
  output Co
);

  wire n4x1_mux_1_out_7, not_1_out;

  _4x1_mux u_4x1_mux_1 (.S1(S1), .S0(S0), .I0(1'b0), .I1(B), .I2(not_1_out), .I3(1'b1), .out_7(n4x1_mux_1_out_7));
  not not_1 (not_1_out, B);
  full_adder full_adder_1 (.A(A), .B(n4x1_mux_1_out_7), .Cin(Ci), .S(F), .Cout(Co));
endmodule

// 4 AU
module _4bit_AU (
  input  Ci,
  input  [3:0] A,
  input  [3:0] B,
  input  S1,
  input  S0,
  output [3:0] F,
  output V,
  output Co
);

  wire n1bit_au_1_co, n1bit_au_2_co, n1bit_au_3_co;

  _1bit_AU u_1bit_au_1 (.Ci(Ci), .A(A[0]), .B(B[0]), .S1(S1), .S0(S0), .F(F[0]), .Co(n1bit_au_1_co));
  _1bit_AU u_1bit_au_2 (.Ci(n1bit_au_1_co), .A(A[1]), .B(B[1]), .S1(S1), .S0(S0), .F(F[1]), .Co(n1bit_au_2_co));
  _1bit_AU u_1bit_au_3 (.Ci(n1bit_au_2_co), .A(A[2]), .B(B[2]), .S1(S1), .S0(S0), .F(F[2]), .Co(n1bit_au_3_co));
  _1bit_AU u_1bit_au_4 (.Ci(n1bit_au_3_co), .A(A[3]), .B(B[3]), .S1(S1), .S0(S0), .F(F[3]), .Co(Co));
  xor xor_1 (V, n1bit_au_3_co, Co);
endmodule

// 8 AU
module _8bit_AU (
  input  Ci,
  input  [7:0] A,
  input  [7:0] B,
  input  S1,
  input  S0,
  output [7:0] F,
  output V,
  output Co
);

  wire n4bit_au_1_co;

  _4bit_AU u_4bit_au_1 (.Ci(Ci), .A(A[3:0]), .B(B[3:0]), .S1(S1), .S0(S0), .F(F[3:0]), .Co(n4bit_au_1_co));  // open: V
  _4bit_AU u_4bit_au_2 (.Ci(n4bit_au_1_co), .A(A[7:4]), .B(B[7:4]), .S1(S1), .S0(S0), .F(F[7:4]), .Co(Co), .V(V));
endmodule

module _4bit_ALU (
  input  [3:0] A,
  input  [3:0] B,
  input  S2,
  input  S1,
  input  S0,
  input  Ci,
  input  H1,
  input  H0,
  output [3:0] F,
  output Z,
  output S,
  output V,
  output Co
);

  wire [3:0] n4bit_2x1_mux_1_o, n4bit_au_1_f, n4bit_lu_1_f;

  _4bit_LU u_4bit_lu_1 (.A(A), .B(B), .S1(S1), .S0(S0), .F(n4bit_lu_1_f));
  _4bit_2x1_mux u_4bit_2x1_mux_1 (.A(n4bit_lu_1_f), .B(n4bit_au_1_f), .S(S2), .O(n4bit_2x1_mux_1_o));
  _4bit_AU u_4bit_au_1 (.Ci(Ci), .A(A), .B(B), .S1(S1), .S0(S0), .F(n4bit_au_1_f), .Co(Co), .V(V));
  _4bit_shifter u_4bit_shifter_1 (.I(n4bit_2x1_mux_1_o), .S1(H1), .S0(H0), .SLin(1'b0), .SRin(1'b0), .out_6(F));
  nor nor_1 (Z, F[0], F[1], F[2], F[3]);

  assign S = F[3];
endmodule

// 4 LU
module _4bit_ALU_2 (
  input  [3:0] A,
  input  [3:0] B,
  input  S2,
  input  S1,
  input  S0,
  input  H1,
  input  Ci,
  input  H0,
  output V,
  output Co,
  output Z,
  output S,
  output [3:0] F
);

  wire [3:0] n4bit_2x1_mux_1_o, n4bit_au_1_f, n4bit_lu_1_f;

  _4bit_AU u_4bit_au_1 (.Ci(Ci), .A(A), .B(B), .S1(S1), .S0(S0), .F(n4bit_au_1_f), .Co(Co), .V(V));
  _4bit_2x1_mux u_4bit_2x1_mux_1 (.A(n4bit_au_1_f), .B(n4bit_lu_1_f), .S(S2), .O(n4bit_2x1_mux_1_o));
  _4bit_LU u_4bit_lu_1 (.A(A), .B(B), .S1(S1), .S0(S0), .F(n4bit_lu_1_f));
  _4bit_shifter u_4bit_shifter_1 (.I(n4bit_2x1_mux_1_o), .S1(H1), .S0(H0), .SLin(1'b0), .SRin(1'b0), .out_6(F));
  nor nor_1 (Z, F[0], F[1], F[2], F[3]);

  assign S = F[3];
endmodule

module _4bit_ALU_3 (
  input  [3:0] A,
  input  [3:0] B,
  input  S2,
  input  S1,
  input  S0,
  input  Ci,
  output V,
  output Co,
  output Z,
  output S,
  output [3:0] F
);

  wire [3:0] n4bit_2x1_mux_2_o, n4bit_au_1_f, n4bit_lu_1_f, n4bit_shifter_1_out_6;

  _4bit_AU u_4bit_au_1 (.Ci(Ci), .A(A), .B(B), .S1(S1), .S0(S0), .F(n4bit_au_1_f), .Co(Co), .V(V));
  _4bit_LU u_4bit_lu_1 (.A(A), .B(B), .S1(S1), .S0(S0), .F(n4bit_lu_1_f));
  _4bit_shifter u_4bit_shifter_1 (.I(A), .S1(S1), .S0(S0), .SLin(1'b0), .SRin(1'b0), .out_6(n4bit_shifter_1_out_6));
  _4bit_2x1_mux u_4bit_2x1_mux_1 (.A(n4bit_au_1_f), .B(n4bit_2x1_mux_2_o), .S(S2), .O(F));
  _4bit_2x1_mux u_4bit_2x1_mux_2 (.A(n4bit_lu_1_f), .B(n4bit_shifter_1_out_6), .S(Ci), .O(n4bit_2x1_mux_2_o));
  nor nor_1 (Z, F[0], F[1], F[2], F[3]);

  assign S = F[3];
endmodule

// 8 ALU
module _8bit_ALU (
  input  [7:0] A,
  input  [7:0] B,
  input  S2,
  input  S1,
  input  S0,
  input  H1,
  input  Ci,
  input  H0,
  output V,
  output Co,
  output Z,
  output S,
  output [7:0] F
);

  wire [7:0] n8bit_2x1_mux_1_o, n8bit_au_1_f, n8bit_lu_1_f;

  _8bit_AU u_8bit_au_1 (.Ci(Ci), .A(A), .B(B), .S1(S1), .S0(S0), .F(n8bit_au_1_f), .Co(Co), .V(V));
  _8bit_LU u_8bit_lu_1 (.A(A), .B(B), .S1(S1), .S0(S0), .F(n8bit_lu_1_f));
  _8bit_2x1_mux u_8bit_2x1_mux_1 (.A(n8bit_au_1_f), .B(n8bit_lu_1_f), .S(S2), .O(n8bit_2x1_mux_1_o));
  _8bit_shifter u_8bit_shifter_1 (.SLin(1'b0), .I(n8bit_2x1_mux_1_o), .SRin(1'b0), .S1(H1), .S0(H0), .O(F));
  nor nor_1 (Z, F[0], F[1], F[2], F[3], F[4], F[5], F[6], F[7]);

  assign S = F[7];
endmodule

// 8 ALU
module _8bit_ALU_2 (
  input  [7:0] A,
  input  [7:0] B,
  input  [5:0] Sel,
  output V,
  output Co,
  output Z,
  output S,
  output [7:0] F
);

  wire [7:0] n8bit_2x1_mux_1_o, n8bit_au_1_f, n8bit_lu_1_f;

  _8bit_AU u_8bit_au_1 (.Ci(Sel[2]), .A(A), .B(B), .S1(Sel[4]), .S0(Sel[3]), .F(n8bit_au_1_f), .Co(Co), .V(V));
  _8bit_LU u_8bit_lu_1 (.A(A), .B(B), .S1(Sel[4]), .S0(Sel[3]), .F(n8bit_lu_1_f));
  _8bit_2x1_mux u_8bit_2x1_mux_1 (.A(n8bit_au_1_f), .B(n8bit_lu_1_f), .S(Sel[5]), .O(n8bit_2x1_mux_1_o));
  _8bit_shifter u_8bit_shifter_1 (.SLin(1'b0), .I(n8bit_2x1_mux_1_o), .SRin(1'b0), .S1(Sel[1]), .S0(Sel[0]), .O(F));
  nor nor_1 (Z, F[0], F[1], F[2], F[3], F[4], F[5], F[6], F[7]);

  assign S = F[7];

  // Notes on the sheet:
  //   S2 S1 S0 Ci H1 H0
endmodule

// 8 ALU
module _8bit_ALU_3 (
  input  [7:0] A,
  input  [7:0] B,
  input  [3:0] Sel,
  output V,
  output Co,
  output Z,
  output S,
  output [7:0] F
);

  wire [7:0] n8bit_2x1_mux_1_o, n8bit_au_1_f, n8bit_lu_1_f, n8bit_shifter_1_o;

  _8bit_AU u_8bit_au_1 (.Ci(Sel[0]), .A(A), .B(B), .S1(Sel[2]), .S0(Sel[1]), .F(n8bit_au_1_f), .Co(Co), .V(V));
  _8bit_LU u_8bit_lu_1 (.A(A), .B(B), .S1(Sel[2]), .S0(Sel[1]), .F(n8bit_lu_1_f));
  _8bit_shifter u_8bit_shifter_1 (.SLin(1'b0), .I(A), .SRin(1'b0), .S1(Sel[2]), .S0(Sel[1]), .O(n8bit_shifter_1_o));
  _8bit_2x1_mux u_8bit_2x1_mux_1 (.A(n8bit_lu_1_f), .B(n8bit_shifter_1_o), .S(Sel[0]), .O(n8bit_2x1_mux_1_o));
  _8bit_2x1_mux u_8bit_2x1_mux_2 (.A(n8bit_au_1_f), .B(n8bit_2x1_mux_1_o), .S(Sel[3]), .O(F));
  nor nor_1 (Z, F[0], F[1], F[2], F[3], F[4], F[5], F[6], F[7]);

  assign S = F[7];

  // Notes on the sheet:
  //   S2 S1 S0 Ci
endmodule

// 4 2x1
module _4bit_2x1_mux (
  input  [3:0] A,
  input  [3:0] B,
  input  S,
  output [3:0] O
);

  _2x1_mux u_2x1_mux_1 (.S(S), .I0(A[0]), .I1(B[0]), .O(O[0]));
  _2x1_mux u_2x1_mux_2 (.S(S), .I0(A[1]), .I1(B[1]), .O(O[1]));
  _2x1_mux u_2x1_mux_3 (.S(S), .I0(A[2]), .I1(B[2]), .O(O[2]));
  _2x1_mux u_2x1_mux_4 (.S(S), .I0(A[3]), .I1(B[3]), .O(O[3]));
endmodule

// 8 2x1
module _8bit_2x1_mux (
  input  [7:0] A,
  input  [7:0] B,
  input  S,
  output [7:0] O
);

  _4bit_2x1_mux u_4bit_2x1_mux_1 (.A(A[3:0]), .B(B[3:0]), .S(S), .O(O[3:0]));
  _4bit_2x1_mux u_4bit_2x1_mux_2 (.A(A[7:4]), .B(B[7:4]), .S(S), .O(O[7:4]));
endmodule

module data_path___status (
  input  acld,
  input  [1:0] R,
  input  pcld,
  input  [3:0] ALU,
  input  iraddrld,
  input  mbrld,
  input  stld,
  input  M,
  input  marld,
  input  iropld,
  input  in_11,
  input  rw,
  input  in_13
);

  wire clock_1_out, not_1_out;
  wire [3:0] n8bit_alu_3_1_v;
  wire [7:0] AC_q, controlled_buffer_1_out, IR_Addr_q, MAR_q, MBR_q, multiplexer_1_out, multiplexer_2_out,
       n8bit_alu_3_1_f, PC_q;

  Multiplexer #(.width(8), .enable("false")) multiplexer_1 (
    .in0(n8bit_alu_3_1_f), .in1(controlled_buffer_1_out), .out(multiplexer_1_out), .sel(M));
  Clock clock_1 (.out(clock_1_out));
  Register AC (.D(n8bit_alu_3_1_f), .en(acld), .Q(AC_q), .clk(clock_1_out), .clr(in_11));
  Register PC (.D(n8bit_alu_3_1_f), .en(pcld), .Q(PC_q), .clk(clock_1_out), .clr(in_11));
  Register IR_Addr (.D(n8bit_alu_3_1_f), .en(iraddrld), .Q(IR_Addr_q), .clk(clock_1_out), .clr(in_11));
  Register MBR (.D(multiplexer_1_out), .en(mbrld), .Q(MBR_q), .clk(clock_1_out), .clr(in_11));
  Register MAR (.D(n8bit_alu_3_1_f), .en(marld), .Q(MAR_q), .clk(clock_1_out), .clr(in_11));
  assign controlled_buffer_1_out = not_1_out ? MBR_q : 8'bz;  // Controlled_Buffer controlled_buffer_1
  not not_1 (not_1_out, rw);
  Multiplexer #(.select(2), .width(8), .enable("false")) multiplexer_2 (
    .in0(AC_q), .in1(PC_q), .in2(IR_Addr_q), .in3(MBR_q), .out(multiplexer_2_out), .sel(R));
  // Probe on multiplexer_2_out
  // Probe on MBR_q
  Register IR_Op (.D(MBR_q), .en(iropld), .clk(clock_1_out), .clr(in_11));  // open: Q
  // Probe on n8bit_alu_3_1_f
  _8bit_ALU_3 u_8bit_alu_3_1 (
    .A(multiplexer_2_out), .B(MBR_q), .Sel(ALU), .V(n8bit_alu_3_1_v[0]), .Co(n8bit_alu_3_1_v[1]),
    .Z(n8bit_alu_3_1_v[2]), .S(n8bit_alu_3_1_v[3]), .F(n8bit_alu_3_1_f));
  Register #(.width(4)) status (.D(n8bit_alu_3_1_v), .en(stld), .clk(clock_1_out), .clr(in_11));  // open: Q
  RAM ram_1 (.addr(MAR_q), .data(controlled_buffer_1_out), .sel(in_13), .clk(clock_1_out), .ld(rw));  // open: clr

  // Notes on the sheet:
  //   RAM
endmodule

module data_path (
  input  acld,
  input  [1:0] R,
  input  pcld,
  input  [3:0] ALU,
  input  iraddrld,
  input  mbrld,
  input  M,
  input  marld,
  input  iropld,
  input  in_10,
  input  rw,
  input  in_12
);

  wire clock_1_out, not_1_out;
  wire [7:0] AC_q, controlled_buffer_1_out, IR_Addr_q, MAR_q, MBR_q, multiplexer_1_out, multiplexer_2_out,
       n8bit_alu_3_1_f, PC_q;

  Multiplexer #(.width(8), .enable("false")) multiplexer_1 (
    .in0(n8bit_alu_3_1_f), .in1(controlled_buffer_1_out), .out(multiplexer_1_out), .sel(M));
  Clock clock_1 (.out(clock_1_out));
  Register AC (.D(n8bit_alu_3_1_f), .en(acld), .Q(AC_q), .clk(clock_1_out), .clr(in_10));
  Register PC (.D(n8bit_alu_3_1_f), .en(pcld), .Q(PC_q), .clk(clock_1_out), .clr(in_10));
  Register IR_Addr (.D(n8bit_alu_3_1_f), .en(iraddrld), .Q(IR_Addr_q), .clk(clock_1_out), .clr(in_10));
  Register MBR (.D(multiplexer_1_out), .en(mbrld), .Q(MBR_q), .clk(clock_1_out), .clr(in_10));
  Register MAR (.D(n8bit_alu_3_1_f), .en(marld), .Q(MAR_q), .clk(clock_1_out), .clr(in_10));
  assign controlled_buffer_1_out = not_1_out ? MBR_q : 8'bz;  // Controlled_Buffer controlled_buffer_1
  not not_1 (not_1_out, rw);
  Multiplexer #(.select(2), .width(8), .enable("false")) multiplexer_2 (
    .in0(AC_q), .in1(PC_q), .in2(IR_Addr_q), .in3(MBR_q), .out(multiplexer_2_out), .sel(R));
  // Probe on multiplexer_2_out
  // Probe on MBR_q
  Register IR_Op (.D(MBR_q), .en(iropld), .clk(clock_1_out), .clr(in_10));  // open: Q
  // Probe on n8bit_alu_3_1_f
  _8bit_ALU_3 u_8bit_alu_3_1 (.A(multiplexer_2_out), .B(MBR_q), .Sel(ALU), .F(n8bit_alu_3_1_f));  // open: V, Co, Z, S
  RAM ram_1 (.addr(MAR_q), .data(controlled_buffer_1_out), .sel(in_12), .clk(clock_1_out), .ld(rw));  // open: clr

  // Notes on the sheet:
  //   RAM
endmodule

module simple_data_path (
  input  in_1,
  input  [1:0] in_2,
  input  in_3,
  input  [3:0] in_4,
  input  in_5,
  input  in_6,
  input  in_7,
  input  in_8,
  input  in_9
);

  wire clock_1_out;
  wire [7:0] AC_q, IR_Addr_q, MBR_q, multiplexer_1_out, n8bit_alu_3_1_f, PC_q;

  Clock clock_1 (.out(clock_1_out));
  Register AC (.D(n8bit_alu_3_1_f), .en(in_1), .Q(AC_q), .clk(clock_1_out), .clr(in_9));
  Register PC (.D(n8bit_alu_3_1_f), .en(in_3), .Q(PC_q), .clk(clock_1_out), .clr(in_9));
  Register IR_Addr (.D(n8bit_alu_3_1_f), .en(in_5), .Q(IR_Addr_q), .clk(clock_1_out), .clr(in_9));
  Register MBR (.D(n8bit_alu_3_1_f), .en(in_6), .Q(MBR_q), .clk(clock_1_out), .clr(in_9));
  Register MAR (.D(n8bit_alu_3_1_f), .en(in_7), .clk(clock_1_out), .clr(in_9));  // open: Q
  Multiplexer #(.select(2), .width(8), .enable("false")) multiplexer_1 (
    .in0(AC_q), .in1(PC_q), .in2(IR_Addr_q), .in3(MBR_q), .out(multiplexer_1_out), .sel(in_2));
  Register IR_Op (.D(MBR_q), .en(in_8), .clk(clock_1_out), .clr(in_9));  // open: Q
  // Probe on n8bit_alu_3_1_f
  _8bit_ALU_3 u_8bit_alu_3_1 (.A(multiplexer_1_out), .B(MBR_q), .Sel(in_4), .F(n8bit_alu_3_1_f));  // open: V, Co, Z, S
endmodule

module _4_register___ALU (
  input  in_1,
  input  [1:0] in_2,
  input  in_3,
  input  [3:0] in_4,
  input  in_5,
  input  in_6,
  input  in_7
);

  wire clock_1_out;
  wire [7:0] AC_q, IR_Addr_q, MBR_q, multiplexer_1_out, n8bit_alu_3_1_f, PC_q;

  Clock clock_1 (.out(clock_1_out));
  Register AC (.D(n8bit_alu_3_1_f), .en(in_1), .Q(AC_q), .clk(clock_1_out), .clr(in_7));
  Register PC (.D(n8bit_alu_3_1_f), .en(in_3), .Q(PC_q), .clk(clock_1_out), .clr(in_7));
  Register IR_Addr (.D(n8bit_alu_3_1_f), .en(in_5), .Q(IR_Addr_q), .clk(clock_1_out), .clr(in_7));
  Register MBR (.D(n8bit_alu_3_1_f), .en(in_6), .Q(MBR_q), .clk(clock_1_out), .clr(in_7));
  Multiplexer #(.select(2), .width(8), .enable("false")) multiplexer_1 (
    .in0(AC_q), .in1(PC_q), .in2(IR_Addr_q), .in3(MBR_q), .out(multiplexer_1_out), .sel(in_2));
  // Probe on n8bit_alu_3_1_f
  _8bit_ALU_3 u_8bit_alu_3_1 (.A(multiplexer_1_out), .B(MBR_q), .Sel(in_4), .F(n8bit_alu_3_1_f));  // open: V, Co, Z, S
endmodule

module _4_register_data_path (
  input  in_1,
  input  [1:0] in_2,
  input  in_3,
  input  in_4,
  input  in_5,
  input  in_6
);

  wire clock_1_out;
  wire [7:0] AC_q, IR_Addr_q, MBR_q, multiplexer_1_out, PC_q;

  Clock clock_1 (.out(clock_1_out));
  Register AC (.D(multiplexer_1_out), .en(in_1), .Q(AC_q), .clk(clock_1_out), .clr(in_6));
  Register PC (.D(multiplexer_1_out), .en(in_3), .Q(PC_q), .clk(clock_1_out), .clr(in_6));
  Register IR_Addr (.D(multiplexer_1_out), .en(in_4), .Q(IR_Addr_q), .clk(clock_1_out), .clr(in_6));
  Register MBR (.D(multiplexer_1_out), .en(in_5), .Q(MBR_q), .clk(clock_1_out), .clr(in_6));
  Multiplexer #(.select(2), .width(8), .enable("false")) multiplexer_1 (
    .in0(AC_q), .in1(PC_q), .in2(IR_Addr_q), .in3(MBR_q), .out(multiplexer_1_out), .sel(in_2));
  // Probe on multiplexer_1_out
endmodule

module _4_register (
  input  in_1,
  input  in_2,
  input  in_3,
  input  in_4,
  input  in_5
);

  wire clock_1_out;
  wire [7:0] IR_Addr_q;

  Clock clock_1 (.out(clock_1_out));
  Register AC (.D(IR_Addr_q), .en(in_1), .clk(clock_1_out), .clr(in_5));  // open: Q
  Register PC (.D(IR_Addr_q), .en(in_2), .clk(clock_1_out), .clr(in_5));  // open: Q
  Register IR_Addr (.D(IR_Addr_q), .en(in_3), .Q(IR_Addr_q), .clk(clock_1_out), .clr(in_5));
  Register MBR (.D(IR_Addr_q), .en(in_4), .clk(clock_1_out), .clr(in_5));  // open: Q
endmodule

module _2_register (
  input  in_1,
  input  in_2
);

  wire clock_1_out;
  wire [7:0] register_1_q, register_2_q;

  Register register_1 (.D(register_2_q), .en(in_1), .Q(register_1_q), .clk(clock_1_out));  // open: clr
  Clock clock_1 (.out(clock_1_out));
  Register register_2 (.D(register_1_q), .en(in_2), .Q(register_2_q), .clk(clock_1_out));  // open: clr
endmodule

module cpu (
  input  in_1,
  input  in_2
);

  wire acld, clock_1_out, iraddrld, iropld, M, marld, mbrld, not_1_out, pcld, rw, stld;
  wire [1:0] R;
  wire [2:0] cu_fetch_only_1_cnt;
  wire [3:0] ALU, n8bit_alu_3_1_v, status_q;
  wire [7:0] AC_q, controlled_buffer_1_out, IR_Addr_q, IR_Op_q, MAR_q, MBR_q, multiplexer_1_out,
       multiplexer_2_out, n8bit_alu_3_1_f, PC_q;

  // Probe on M
  Multiplexer #(.width(8), .enable("false")) multiplexer_1 (
    .in0(n8bit_alu_3_1_f), .in1(controlled_buffer_1_out), .out(multiplexer_1_out), .sel(M));
  Clock clock_1 (.out(clock_1_out));
  Register AC (.D(n8bit_alu_3_1_f), .en(acld), .Q(AC_q), .clk(clock_1_out), .clr(in_1));
  Register PC (.D(n8bit_alu_3_1_f), .en(pcld), .Q(PC_q), .clk(clock_1_out), .clr(in_1));
  Register IR_Addr (.D(n8bit_alu_3_1_f), .en(iraddrld), .Q(IR_Addr_q), .clk(clock_1_out), .clr(in_1));
  Register MBR (.D(multiplexer_1_out), .en(mbrld), .Q(MBR_q), .clk(clock_1_out), .clr(in_1));
  Register MAR (.D(n8bit_alu_3_1_f), .en(marld), .Q(MAR_q), .clk(clock_1_out), .clr(in_1));
  assign controlled_buffer_1_out = not_1_out ? MBR_q : 8'bz;  // Controlled_Buffer controlled_buffer_1
  not not_1 (not_1_out, rw);
  Multiplexer #(.select(2), .width(8), .enable("false")) multiplexer_2 (
    .in0(AC_q), .in1(PC_q), .in2(IR_Addr_q), .in3(MBR_q), .out(multiplexer_2_out), .sel(R));
  // Probe on multiplexer_2_out
  // Probe on MBR_q
  Register IR_Op (.D(MBR_q), .en(iropld), .Q(IR_Op_q), .clk(clock_1_out), .clr(in_1));
  // Probe on n8bit_alu_3_1_f
  _8bit_ALU_3 u_8bit_alu_3_1 (
    .A(multiplexer_2_out), .B(MBR_q), .Sel(ALU), .V(n8bit_alu_3_1_v[0]), .Co(n8bit_alu_3_1_v[1]),
    .Z(n8bit_alu_3_1_v[2]), .S(n8bit_alu_3_1_v[3]), .F(n8bit_alu_3_1_f));
  // Probe on ALU
  Register #(.width(4)) status (.D(n8bit_alu_3_1_v), .en(stld), .Q(status_q), .clk(clock_1_out), .clr(in_1));
  // Probe on R
  // Probe on cu_fetch_only_1_cnt
  CU_fetch_only cu_fetch_only_1 (
    .Ck(clock_1_out), .RST(in_1), .st(status_q), .IR_Op(IR_Op_q), .M(M), .ALU(ALU), .rw(rw), .R(R),
    .LDs({acld, pcld, iraddrld, mbrld, marld, iropld, stld}), .cnt(cu_fetch_only_1_cnt));
  RAM ram_1 (.addr(MAR_q), .data(controlled_buffer_1_out), .sel(in_2), .clk(clock_1_out), .ld(rw));  // open: clr

  // Notes on the sheet:
  //   RAM
endmodule

module CU (
  input  Ck,
  input  RST,
  input  [3:0] st,
  input  [7:0] IR_Op,
  output rw,
  output [1:0] R,
  output [2:0] cnt,
  output M,
  output [3:0] ALU,
  output [6:0] LDs
);

  wire not_1_out, T0, T1;

  Counter #(.width(3), .max('h7)) u_cnt (.Q(cnt), .clk(not_1_out), .clr(RST));  // open: load, D, count, carry
  not not_1 (not_1_out, Ck);
  Decoder #(.select(3), .disabled(0), .enable("false")) decoder_1 (
    .out0(T0), .out1(T1), .out2(LDs[1]), .out3(LDs[4]), .sel(cnt));  // open: out4, out5, out6, out7
  or or_1 (LDs[2], T0, T1);
  or or_2 (ALU[0], T1, LDs[1]);

  assign ALU[3:1] = 3'b000;
  assign {LDs[6:5], LDs[3], LDs[0]} = {1'b0, {2{ALU[0]}}, 1'b0};
  assign M = ALU[0];
  assign R = {LDs[4], 1'b1};
  assign rw = 1'b1;

  // Other names for the same wires on the sheet: T2 = LDs[1]; T3 = LDs[4]
endmodule

// CU p2
module CU_partial_2 (
  input  Ck,
  input  RST,
  input  [3:0] st,
  input  [7:0] IR_Op,
  output [1:0] R,
  output [2:0] cnt,
  output M,
  output [5:0] ALU,
  output [5:0] LDs,
  output rw
);

  wire AC2BR, ADD, ADD_T4, ADD_T5, ADD_T6, AND, and_27_out, AND_T4, AND_T5, AND_T6, BR2AC, BZ, BZ_T4,
       IRAD2AR, IRAD2PC, JMP, JMP_T4, LDA, LDA_T4, LDA_T5, NOP, NOT, not_1_out, NOT_T4, OR, OR_T4, OR_T5,
       OR_T6, READ, SHL, SHR, STR, STR_T4, STR_T6, SUB, SUB_T4, SUB_T5, SUB_T6, T0, T1, T4, T5, T6, T7, uXOR,
       XOR, XOR_T4, XOR_T5;

  Counter #(.width(3), .max('h7)) u_cnt (.Q(cnt), .clk(not_1_out), .clr(RST));  // open: load, D, count, carry
  not not_1 (not_1_out, Ck);
  and and_1 (NOT_T4, NOT, T4);
  and and_2 (ALU[0], SHR, T4);
  and and_3 (BZ_T4, BZ, T4);
  and and_4 (LDA_T4, LDA, T4);
  and and_5 (LDA_T5, LDA, T5);
  and and_6 (BR2AC, LDA, T6);
  and and_7 (SUB_T4, SUB, T4);
  and and_8 (SUB_T5, SUB, T5);
  and and_9 (SUB_T6, SUB, T6);
  and and_10 (OR_T4, OR, T4);
  and and_11 (OR_T5, OR, T5);
  and and_12 (OR_T6, OR, T6);
  and and_13 (STR_T4, STR, T4);
  and and_14 (AC2BR, STR, T5);
  and and_15 (STR_T6, STR, T6);
  Decoder #(.select(3), .disabled(0), .enable("false")) decoder_1 (
    .out0(T0), .out1(T1), .out2(LDs[0]), .out3(LDs[3]), .out4(T4), .out5(T5), .out6(T6), .out7(T7), .sel(cnt));
  Decoder #(.select(4), .enable("false")) decoder_2 (
    .out0(NOP), .out1(NOT), .out2(SHL), .out3(SHR), .out4(JMP), .out5(BZ), .out8(LDA), .out9(ADD),
    .out10(SUB), .out11(AND), .out12(OR), .out13(XOR), .out15(STR), .sel(IR_Op[7:4]));  // open: out6, out7, out14
  and and_16 (ALU[1], SHL, T4);
  and and_17 (JMP_T4, JMP, T4);
  and and_18 (ADD_T4, ADD, T4);
  and and_19 (ADD_T5, ADD, T5);
  and and_20 (ADD_T6, ADD, T6);
  and and_21 (AND_T4, AND, T4);
  and and_22 (AND_T5, AND, T5);
  and and_23 (AND_T6, AND, T6);
  and and_24 (XOR_T4, XOR, T4);
  and and_25 (XOR_T5, XOR, T5);
  and and_26 (uXOR, XOR, T6);
  or or_1 (IRAD2PC, JMP_T4, and_27_out);
  and and_27 (and_27_out, BZ_T4, st[2]);
  or or_2 (IRAD2AR, LDA_T4, ADD_T4, SUB_T4, AND_T4, OR_T4, XOR_T4, STR_T4);
  or or_3 (READ, LDA_T5, ADD_T5, SUB_T5, AND_T5, OR_T5, XOR_T5);
  or or_4 (ALU[2], T1, SUB_T6, LDs[0]);
  or or_5 (ALU[3], ADD_T6, OR_T6, NOT_T4);
  or or_6 (ALU[4], SUB_T6, uXOR, NOT_T4);
  or or_7 (ALU[5], AND_T6, OR_T6, uXOR, NOT_T4);
  or or_8 (LDs[5], BR2AC, ADD_T6, SUB_T6, AND_T6, OR_T6, uXOR, NOT_T4, ALU[1], ALU[0]);
  or or_9 (LDs[1], T0, IRAD2AR, T1);
  or or_10 (LDs[2], T1, READ, AC2BR, LDs[0]);
  or or_11 (LDs[4], T1, IRAD2PC, LDs[0]);
  not not_2 (rw, STR_T6);
  or or_12 (R[0], T0, T1, LDs[0], LDs[3], BR2AC);
  or or_13 (R[1], LDs[3], IRAD2AR, BR2AC, IRAD2PC);
  or or_14 (M, T1, LDs[0], READ);

  // Other names for the same wires on the sheet: SHR_T4 = ALU[0]; uSHR = ALU[0]; SHL_T4 = ALU[1]; uSHL = ALU[1];
  //   LDA_T6 = BR2AC; T2 = LDs[0]; T3 = LDs[3]; V = st[0]; C = st[1]; Z = st[2]; S = st[3]; STR_T5 = AC2BR;
  //   uADD = ADD_T6; uAND = AND_T6; uNOT = NOT_T4; uOR = OR_T6; uSUB = SUB_T6; XOR_T6 = uXOR; WRITE = STR_T6
endmodule

// CU p3
module CU_partial_3 (
  input  Ck,
  input  RST,
  input  [3:0] st,
  input  [7:0] IR_Op,
  output [1:0] R,
  output [2:0] cnt,
  output M,
  output [5:0] ALU,
  output [5:0] LDs,
  output rw
);

  wire AC2BR, ADD, ADD_T4, ADD_T5, AND, BNZ, BR2AC, BZ, IRAD2AR, IRAD2PC, JMP, LDA, LDA_T4, LDA_T5, NOP, NOT,
       not_1_out, OR, READ, SHL, SHR, STR, STR_T4, STR_T6, SUB, T0, T1, T4, T5, T6, T7, XOR;

  Counter #(.width(3), .max('h7)) u_cnt (.Q(cnt), .clk(not_1_out), .clr(RST));  // open: load, D, count, carry
  not not_1 (not_1_out, Ck);
  or or_1 (IRAD2AR, ADD_T4, LDA_T4, STR_T4);
  or or_2 (READ, ADD_T5, LDA_T5);
  Decoder #(.select(3), .disabled(0), .enable("false")) decoder_1 (
    .out0(T0), .out1(T1), .out2(LDs[0]), .out3(LDs[3]), .out4(T4), .out5(T5), .out6(T6), .out7(T7), .sel(cnt));
  Decoder #(.select(4), .enable("false")) decoder_2 (
    .out0(NOP), .out1(NOT), .out2(SHL), .out3(SHR), .out4(JMP), .out5(BZ), .out6(BNZ), .out8(LDA),
    .out9(ADD), .out10(SUB), .out11(AND), .out12(OR), .out13(XOR), .out15(STR), .sel(IR_Op[7:4]));  // open: out7, out14
  and and_1 (IRAD2PC, JMP, T4);
  and and_2 (LDA_T4, LDA, T4);
  and and_3 (LDA_T5, LDA, T5);
  and and_4 (BR2AC, LDA, T6);
  and and_5 (ADD_T4, ADD, T4);
  and and_6 (ADD_T5, ADD, T5);
  and and_7 (ALU[3], ADD, T6);
  and and_8 (STR_T4, STR, T4);
  and and_9 (AC2BR, STR, T5);
  and and_10 (STR_T6, STR, T6);
  or or_3 (R[0], T0, T1, LDs[0], LDs[3], BR2AC);
  or or_4 (R[1], LDs[3], IRAD2AR, IRAD2PC, BR2AC);
  or or_5 (M, T1, READ, LDs[0]);
  or or_6 (ALU[2], T1, LDs[0]);
  or or_7 (LDs[5], BR2AC, ALU[3]);
  or or_8 (LDs[1], T0, IRAD2AR, T1);
  or or_9 (LDs[2], T1, READ, AC2BR, LDs[0]);
  or or_10 (LDs[4], T1, IRAD2PC, LDs[0]);
  not not_2 (rw, STR_T6);

  assign {ALU[5:4], ALU[1:0]} = 4'b0000;

  // Other names for the same wires on the sheet: ADD_T6 = ALU[3]; uADD = ALU[3]; JMP_T4 = IRAD2PC; LDA_T6 = BR2AC;
  //   T2 = LDs[0]; T3 = LDs[3]; V = st[0]; C = st[1]; Z = st[2]; S = st[3]; STR_T5 = AC2BR; WRITE = STR_T6
endmodule

// CU fo
module CU_fetch_only (
  input  Ck,
  input  RST,
  input  [3:0] st,
  input  [7:0] IR_Op,
  output M,
  output [3:0] ALU,
  output rw,
  output [1:0] R,
  output [6:0] LDs,
  output [2:0] cnt
);

  wire not_1_out, T0, T1;

  Counter #(.width(3), .max('h7)) u_cnt (.Q(cnt), .clk(not_1_out), .clr(RST));  // open: load, D, count, carry
  not not_1 (not_1_out, Ck);
  Decoder #(.select(3), .disabled(0), .enable("false")) decoder_1 (
    .out0(T0), .out1(T1), .out2(LDs[1]), .out3(LDs[4]), .sel(cnt));  // open: out4, out5, out6, out7
  or or_1 (ALU[0], T1, LDs[1]);
  or or_2 (LDs[2], T0, T1);

  assign ALU[3:1] = 3'b000;
  assign {LDs[6:5], LDs[3], LDs[0]} = {1'b0, {2{ALU[0]}}, 1'b0};
  assign M = ALU[0];
  assign R = {LDs[4], 1'b1};
  assign rw = 1'b1;

  // Other names for the same wires on the sheet: T2 = LDs[1]; T3 = LDs[4]
endmodule

// CU 4inst
module CU_4inst_only (
  input  Ck,
  input  RST,
  input  [3:0] st,
  input  [7:0] IR_Op,
  output [1:0] R,
  output [2:0] cnt,
  output M,
  output [3:0] ALU,
  output [6:0] LDs,
  output rw
);

  wire AC2BR, ADD, ADD_T4, ADD_T5, AND, BNZ, BR2AC, BZ, IRAD2AR, IRAD2PC, JMP, LDA, LDA_T4, LDA_T5, NOP, NOT,
       not_1_out, OR, READ, SHL, SHR, STR, STR_T4, STR_T6, SUB, T0, T1, T4, T5, T6, T7, XOR;

  Counter #(.width(3), .max('h7)) u_cnt (.Q(cnt), .clk(not_1_out), .clr(RST));  // open: load, D, count, carry
  not not_1 (not_1_out, Ck);
  or or_1 (IRAD2AR, ADD_T4, LDA_T4, STR_T4);
  or or_2 (READ, ADD_T5, LDA_T5);
  Decoder #(.select(3), .disabled(0), .enable("false")) decoder_1 (
    .out0(T0), .out1(T1), .out2(LDs[1]), .out3(LDs[4]), .out4(T4), .out5(T5), .out6(T6), .out7(T7), .sel(cnt));
  Decoder #(.select(4), .enable("false")) decoder_2 (
    .out0(NOP), .out1(NOT), .out2(SHL), .out3(SHR), .out4(JMP), .out5(BZ), .out6(BNZ), .out8(LDA),
    .out9(ADD), .out10(SUB), .out11(AND), .out12(OR), .out13(XOR), .out15(STR), .sel(IR_Op[7:4]));  // open: out7, out14
  and and_1 (IRAD2PC, JMP, T4);
  and and_2 (LDA_T4, LDA, T4);
  and and_3 (LDA_T5, LDA, T5);
  and and_4 (BR2AC, LDA, T6);
  and and_5 (ADD_T4, ADD, T4);
  and and_6 (ADD_T5, ADD, T5);
  and and_7 (ALU[1], ADD, T6);
  and and_8 (STR_T4, STR, T4);
  and and_9 (AC2BR, STR, T5);
  and and_10 (STR_T6, STR, T6);
  or or_3 (R[0], T0, T1, LDs[1], LDs[4], BR2AC);
  or or_4 (R[1], LDs[4], IRAD2AR, IRAD2PC, BR2AC);
  or or_5 (M, T1, READ, LDs[1]);
  or or_6 (ALU[0], T1, LDs[1]);
  or or_7 (LDs[6], BR2AC, ALU[1]);
  or or_8 (LDs[2], T0, IRAD2AR, T1);
  or or_9 (LDs[3], T1, READ, AC2BR, LDs[1]);
  or or_10 (LDs[5], T1, IRAD2PC, LDs[1]);
  not not_2 (rw, STR_T6);

  assign ALU[3:2] = 2'b00;
  assign LDs[0] = LDs[6];

  // Other names for the same wires on the sheet: ADD_T6 = ALU[1]; uADD = ALU[1]; JMP_T4 = IRAD2PC; LDA_T6 = BR2AC;
  //   T2 = LDs[1]; T3 = LDs[4]; V = st[0]; C = st[1]; Z = st[2]; S = st[3]; STR_T5 = AC2BR; WRITE = STR_T6
endmodule

module midterm_fri3 (
  input  iraddrld,
  input  [1:0] R,
  input  acld,
  input  [3:0] ALU,
  input  pcld,
  input  mbrld,
  input  stld,
  input  M,
  input  marld,
  input  iropld,
  input  in_11,
  input  rw,
  input  in_13
);

  wire clock_1_out, not_1_out;
  wire [3:0] n8bit_alu_3_1_v;
  wire [7:0] AC_q, controlled_buffer_1_out, IR_Addr_q, MAR_q, MBR_q, multiplexer_1_out, multiplexer_2_out,
       n8bit_alu_3_1_f, PC_q;

  Multiplexer #(.width(8), .enable("false")) multiplexer_1 (
    .in0(n8bit_alu_3_1_f), .in1(controlled_buffer_1_out), .out(multiplexer_1_out), .sel(M));
  Clock clock_1 (.out(clock_1_out));
  Register IR_Addr (.D(n8bit_alu_3_1_f), .en(iraddrld), .Q(IR_Addr_q), .clk(clock_1_out), .clr(in_11));
  Register AC (.D(n8bit_alu_3_1_f), .en(acld), .Q(AC_q), .clk(clock_1_out), .clr(in_11));
  Register PC (.D(n8bit_alu_3_1_f), .en(pcld), .Q(PC_q), .clk(clock_1_out), .clr(in_11));
  Register MBR (.D(multiplexer_1_out), .en(mbrld), .Q(MBR_q), .clk(clock_1_out), .clr(in_11));
  Register MAR (.D(n8bit_alu_3_1_f), .en(marld), .Q(MAR_q), .clk(clock_1_out), .clr(in_11));
  assign controlled_buffer_1_out = not_1_out ? MBR_q : 8'bz;  // Controlled_Buffer controlled_buffer_1
  not not_1 (not_1_out, rw);
  Multiplexer #(.select(2), .width(8), .enable("false")) multiplexer_2 (
    .in0(IR_Addr_q), .in1(AC_q), .in2(PC_q), .in3(MBR_q), .out(multiplexer_2_out), .sel(R));
  // Probe on multiplexer_2_out
  // Probe on MBR_q
  Register IR_Op (.D(MBR_q), .en(iropld), .clk(clock_1_out), .clr(in_11));  // open: Q
  // Probe on n8bit_alu_3_1_f
  _8bit_ALU_3 u_8bit_alu_3_1 (
    .A(multiplexer_2_out), .B(MBR_q), .Sel(ALU), .V(n8bit_alu_3_1_v[0]), .Co(n8bit_alu_3_1_v[1]),
    .Z(n8bit_alu_3_1_v[2]), .S(n8bit_alu_3_1_v[3]), .F(n8bit_alu_3_1_f));
  Register #(.width(4)) status (.D(n8bit_alu_3_1_v), .en(stld), .clk(clock_1_out), .clr(in_11));  // open: Q
  RAM ram_1 (.addr(MAR_q), .data(controlled_buffer_1_out), .sel(in_13), .clk(clock_1_out), .ld(rw));  // open: clr

  // Notes on the sheet:
  //   RAM
endmodule

module midterm_fri5 (
  input  pcld,
  input  [1:0] R,
  input  iraddrld,
  input  [3:0] ALU,
  input  acld,
  input  mbrld,
  input  stld,
  input  M,
  input  marld,
  input  iropld,
  input  in_11,
  input  rw,
  input  in_13
);

  wire clock_1_out, not_1_out;
  wire [3:0] n8bit_alu_3_1_v;
  wire [7:0] AC_q, controlled_buffer_1_out, IR_Addr_q, MAR_q, MBR_q, multiplexer_1_out, multiplexer_2_out,
       n8bit_alu_3_1_f, PC_q;

  Multiplexer #(.width(8), .enable("false")) multiplexer_1 (
    .in0(n8bit_alu_3_1_f), .in1(controlled_buffer_1_out), .out(multiplexer_1_out), .sel(M));
  Clock clock_1 (.out(clock_1_out));
  Register PC (.D(n8bit_alu_3_1_f), .en(pcld), .Q(PC_q), .clk(clock_1_out), .clr(in_11));
  Register IR_Addr (.D(n8bit_alu_3_1_f), .en(iraddrld), .Q(IR_Addr_q), .clk(clock_1_out), .clr(in_11));
  Register AC (.D(n8bit_alu_3_1_f), .en(acld), .Q(AC_q), .clk(clock_1_out), .clr(in_11));
  Register MBR (.D(multiplexer_1_out), .en(mbrld), .Q(MBR_q), .clk(clock_1_out), .clr(in_11));
  Register MAR (.D(n8bit_alu_3_1_f), .en(marld), .Q(MAR_q), .clk(clock_1_out), .clr(in_11));
  assign controlled_buffer_1_out = not_1_out ? MBR_q : 8'bz;  // Controlled_Buffer controlled_buffer_1
  not not_1 (not_1_out, rw);
  Multiplexer #(.select(2), .width(8), .enable("false")) multiplexer_2 (
    .in0(PC_q), .in1(IR_Addr_q), .in2(AC_q), .in3(MBR_q), .out(multiplexer_2_out), .sel(R));
  // Probe on multiplexer_2_out
  // Probe on MBR_q
  Register IR_Op (.D(MBR_q), .en(iropld), .clk(clock_1_out), .clr(in_11));  // open: Q
  // Probe on n8bit_alu_3_1_f
  _8bit_ALU_3 u_8bit_alu_3_1 (
    .A(multiplexer_2_out), .B(MBR_q), .Sel(ALU), .V(n8bit_alu_3_1_v[0]), .Co(n8bit_alu_3_1_v[1]),
    .Z(n8bit_alu_3_1_v[2]), .S(n8bit_alu_3_1_v[3]), .F(n8bit_alu_3_1_f));
  Register #(.width(4)) status (.D(n8bit_alu_3_1_v), .en(stld), .clk(clock_1_out), .clr(in_11));  // open: Q
  RAM ram_1 (.addr(MAR_q), .data(controlled_buffer_1_out), .sel(in_13), .clk(clock_1_out), .ld(rw));  // open: clr

  // Notes on the sheet:
  //   RAM
endmodule

module midterm_fri7 (
  input  iraddrld,
  input  [1:0] R,
  input  pcld,
  input  [3:0] ALU,
  input  acld,
  input  mbrld,
  input  stld,
  input  M,
  input  marld,
  input  iropld,
  input  in_11,
  input  rw,
  input  in_13
);

  wire clock_1_out, not_1_out;
  wire [3:0] n8bit_alu_3_1_v;
  wire [7:0] AC_q, controlled_buffer_1_out, IR_Addr_q, MAR_q, MBR_q, multiplexer_1_out, multiplexer_2_out,
       n8bit_alu_3_1_f, PC_q;

  Multiplexer #(.width(8), .enable("false")) multiplexer_1 (
    .in0(n8bit_alu_3_1_f), .in1(controlled_buffer_1_out), .out(multiplexer_1_out), .sel(M));
  Clock clock_1 (.out(clock_1_out));
  Register IR_Addr (.D(n8bit_alu_3_1_f), .en(iraddrld), .Q(IR_Addr_q), .clk(clock_1_out), .clr(in_11));
  Register PC (.D(n8bit_alu_3_1_f), .en(pcld), .Q(PC_q), .clk(clock_1_out), .clr(in_11));
  Register AC (.D(n8bit_alu_3_1_f), .en(acld), .Q(AC_q), .clk(clock_1_out), .clr(in_11));
  Register MBR (.D(multiplexer_1_out), .en(mbrld), .Q(MBR_q), .clk(clock_1_out), .clr(in_11));
  Register MAR (.D(n8bit_alu_3_1_f), .en(marld), .Q(MAR_q), .clk(clock_1_out), .clr(in_11));
  assign controlled_buffer_1_out = not_1_out ? MBR_q : 8'bz;  // Controlled_Buffer controlled_buffer_1
  not not_1 (not_1_out, rw);
  Multiplexer #(.select(2), .width(8), .enable("false")) multiplexer_2 (
    .in0(IR_Addr_q), .in1(PC_q), .in2(AC_q), .in3(MBR_q), .out(multiplexer_2_out), .sel(R));
  // Probe on multiplexer_2_out
  // Probe on MBR_q
  Register IR_Op (.D(MBR_q), .en(iropld), .clk(clock_1_out), .clr(in_11));  // open: Q
  // Probe on n8bit_alu_3_1_f
  _8bit_ALU_3 u_8bit_alu_3_1 (
    .A(multiplexer_2_out), .B(MBR_q), .Sel(ALU), .V(n8bit_alu_3_1_v[0]), .Co(n8bit_alu_3_1_v[1]),
    .Z(n8bit_alu_3_1_v[2]), .S(n8bit_alu_3_1_v[3]), .F(n8bit_alu_3_1_f));
  Register #(.width(4)) status (.D(n8bit_alu_3_1_v), .en(stld), .clk(clock_1_out), .clr(in_11));  // open: Q
  RAM ram_1 (.addr(MAR_q), .data(controlled_buffer_1_out), .sel(in_13), .clk(clock_1_out), .ld(rw));  // open: clr

  // Notes on the sheet:
  //   RAM
endmodule
