// Logisim project lawlor_fall2011_manual.circ as structural Verilog: 1 circuit, main circuit main
module main (
  input  [1:0] in_1,
  input  [1:0] in_2,
  input  [1:0] Operation_Select,
  input  [7:0] Constant_Input
);

  wire button_1_out, button_2_out, button_3_out;
  wire [7:0] adder_1_out, AND_out, multiplexer_1_out, multiplexer_2_out, multiplexer_3_out, OR_out,
       register_1_q, register_2_q;

  Button button_1 (.out(button_1_out));
  Button button_2 (.out(button_2_out));
  Register register_1 (.D(multiplexer_3_out), .Q(register_1_q), .clk(button_1_out), .clr(button_3_out));  // open: en
  Register register_2 (.D(multiplexer_3_out), .Q(register_2_q), .clk(button_2_out), .clr(button_3_out));  // open: en
  Button button_3 (.out(button_3_out));
  // Probe on register_1_q
  // Probe on register_2_q
  Multiplexer #(.select(2), .width(8), .enable("false")) multiplexer_1 (
    .in0(register_1_q), .in1(register_2_q), .in3(Constant_Input), .out(multiplexer_1_out), .sel(in_1));  // open: in2
  Multiplexer #(.select(2), .width(8), .enable("false")) multiplexer_2 (
    .in0(register_1_q), .in1(register_2_q), .in3(Constant_Input), .out(multiplexer_2_out), .sel(in_2));  // open: in2
  // Probe on multiplexer_1_out
  // Probe on multiplexer_2_out
  assign OR_out = multiplexer_1_out | multiplexer_2_out;  // OR_Gate OR, 8 bits wide
  assign AND_out = multiplexer_1_out & multiplexer_2_out;  // AND_Gate AND, 8 bits wide
  Adder adder_1 (.a(multiplexer_1_out), .b(multiplexer_2_out), .out(adder_1_out));  // open: cin, cout
  // Probe on multiplexer_3_out
  Multiplexer #(.select(2), .width(8)) multiplexer_3 (
    .in0(multiplexer_1_out), .in1(OR_out), .in2(AND_out), .in3(adder_1_out), .out(multiplexer_3_out),
    .sel(Operation_Select));  // open: en

  // Notes on the sheet:
  //   Clock: write to register
  //   Clock: write to register
  //   00 Register
  //   01 Register
  //   Reset: zero register
  //   Operand Output Bus
  //   op 01
  //   op 10
  //   Instruction
  //   Selector
endmodule
