// Logisim project lawlor_fall2012_12bit.circ as structural Verilog: 1 circuit, main circuit main
module main (
  input  Clock,
  input  RESET
);

  wire not_1_out;
  wire [7:0] adder_1_out, adder_2_out, multiplexer_1_out, multiplexer_2_out, multiplier_1_out, register_1_q,
       register_2_q, register_3_q, undriven;
  wire [11:0] rom_1_data;

  Register register_1 (.D(adder_1_out), .en(1'b1), .Q(register_1_q), .clk(Clock), .clr(RESET));
  Adder adder_1 (.a(register_1_q), .b(8'h1), .out(adder_1_out));  // open: cin, cout
  not not_1 (not_1_out, rom_1_data[11]);
  // Probe on adder_1_out
  ROM #(.dataWidth(12)) rom_1 (.addr(register_1_q), .data(rom_1_data), .sel(1'b1));
  Register register_2 (.D(multiplexer_2_out), .en(rom_1_data[11]), .Q(register_2_q), .clk(Clock), .clr(RESET));
  Register register_3 (.D(multiplexer_2_out), .en(not_1_out), .Q(register_3_q), .clk(Clock), .clr(RESET));
  Multiplexer #(.width(8), .enable("false")) multiplexer_1 (
    .in0(register_3_q), .in1(register_2_q), .out(multiplexer_1_out), .sel(rom_1_data[10]));
  // Probe on multiplexer_1_out
  Adder adder_2 (.a(rom_1_data[7:0]), .b(multiplexer_1_out), .out(adder_2_out));  // open: cin, cout
  Multiplier multiplier_1 (.a(rom_1_data[7:0]), .b(multiplexer_1_out), .out(multiplier_1_out));  // open: cin, cout
  // Probe on rom_1_data[9:8]
  // Probe on rom_1_data[7:0]
  // Probe on adder_2_out
  // Probe on multiplexer_2_out
  Multiplexer #(.select(2), .width(8), .enable("false")) multiplexer_2 (
    .in0(rom_1_data[7:0]), .in1(adder_2_out), .in2(undriven), .in3(multiplier_1_out),
    .out(multiplexer_2_out), .sel(rom_1_data[9:8]));

  // Notes on the sheet:
  //   Program Counter
  //   Program ROM
  //   contents of rom_1 (hex, n*v repeats v):
  //   13 804 102 901
  //   Reg1
  //   Reg0
  //   Instruction Decoder
  //   Dest(1):Src(1):Opcode(2):Const(8)
  //   Constant
  //   Arithmetic Unit
endmodule
