// Logisim project lawlor_fall2012_16bit.circ as structural Verilog: 1 circuit, main circuit main
module main (
  input  Clock,
  input  Reset,
  output [15:0] out_3
);

  wire decoder_1_out0, decoder_1_out1, decoder_1_out2, decoder_1_out3, not_1_out;
  wire [3:0] adder_1_out, register_1_q;
  wire [7:0] adder_2_out, multiplexer_1_out, multiplexer_2_out, multiplexer_3_out, multiplier_1_out,
       register_2_q, register_3_q, register_4_q, register_5_q, subtractor_1_out;

  // Probe on out_3[9:8]
  Decoder #(.select(2), .enable("false")) decoder_1 (
    .out0(decoder_1_out0), .out1(decoder_1_out1), .out2(decoder_1_out2), .out3(decoder_1_out3),
    .sel(out_3[9:8]));
  Register #(.width(4)) register_1 (.D(adder_1_out), .en(1'b1), .Q(register_1_q), .clk(Clock), .clr(Reset));
  not not_1 (not_1_out, Clock);
  // Probe on register_1_q
  Register register_2 (.D(multiplexer_3_out), .en(decoder_1_out0), .Q(register_2_q), .clk(not_1_out), .clr(Reset));
  Register register_3 (.D(multiplexer_3_out), .en(decoder_1_out1), .Q(register_3_q), .clk(not_1_out), .clr(Reset));
  Register register_4 (.D(multiplexer_3_out), .en(decoder_1_out2), .Q(register_4_q), .clk(not_1_out), .clr(Reset));
  Register register_5 (.D(multiplexer_3_out), .en(decoder_1_out3), .Q(register_5_q), .clk(not_1_out), .clr(Reset));
  // Probe on adder_1_out
  Adder #(.width(4)) adder_1 (.a(register_1_q), .b(4'b0001), .out(adder_1_out));  // open: cin, cout
  // Probe on out_3[5:4]
  Multiplexer #(.select(2), .width(8), .enable("false")) multiplexer_1 (
    .in0(register_2_q), .in1(register_3_q), .in2(register_4_q), .in3(register_5_q), .out(multiplexer_1_out),
    .sel(out_3[5:4]));
  Multiplexer #(.select(2), .width(8), .enable("false")) multiplexer_2 (
    .in0(register_2_q), .in1(register_3_q), .in2(register_4_q), .in3(register_5_q), .out(multiplexer_2_out),
    .sel(out_3[1:0]));
  // Probe on multiplexer_1_out
  // Probe on out_3[1:0]
  // Probe on multiplexer_2_out
  ROM #(.addrWidth(4), .dataWidth(16)) rom_1 (.addr(register_1_q), .data(out_3), .sel(1'b1));
  // Probe on adder_2_out
  Adder adder_2 (.a(multiplexer_1_out), .b(multiplexer_2_out), .out(adder_2_out));  // open: cin, cout
  // Probe on subtractor_1_out
  Subtractor subtractor_1 (.a(multiplexer_1_out), .b(multiplexer_2_out), .out(subtractor_1_out));  // open: bin, bout
  Multiplier multiplier_1 (.a(multiplexer_1_out), .b(multiplexer_2_out), .out(multiplier_1_out));  // open: cin, cout
  // Probe on multiplier_1_out
  // Probe on out_3[7:0]
  // Probe on out_3[15:12]
  // Probe on multiplexer_3_out
  Multiplexer #(.select(4), .width(8), .enable("false")) multiplexer_3 (
    .in2(subtractor_1_out), .in3(multiplier_1_out), .in10(adder_2_out), .in12(out_3[7:0]),
    .out(multiplexer_3_out), .sel(out_3[15:12]));  // open: in0, in1, in4, in5, in6, in7, in8, in9, in11, in13, in14, in15

  // Notes on the sheet:
  //   Program Counter
  //   Registers
  //   r0
  //   r1
  //   r2
  //   r3
  //   SrcA
  //   Register
  //   Read Ports
  //   SrcB
  //   Program ROM
  //   contents of rom_1 (hex, n*v repeats v):
  //   c205 a322 a233
  //   Constant
  //   Result Bus
  //   Opcode(4):Dest(4):Src1(4):Src2(4)
  //   Opcode(4):Dest(4):Constant(8)
  //   Fetched Instruction
endmodule
