// Logisim project data path.circ as structural Verilog
module data_path (
  input  in_1,
  input  in_2,
  input  [1:0] in_3,
  input  in_4,
  input  in_5,
  input  [1:0] in_6,
  input  in_7,
  input  in_8,
  input  in_9,
  input  in_10,
  input  in_11,
  input  in_12,
  input  in_13
);

  wire clock_1_out, not_1_out;
  wire [7:0] AC_q, adder_1_out, controlled_buffer_1_out, IR_Addr_q, MAR_q, MBR_q, multiplexer_1_out,
       multiplexer_2_out, multiplexer_3_out, PC_q;

  Multiplexer #(.width(8), .enable("false")) multiplexer_1 (
    .in0(adder_1_out), .in1(controlled_buffer_1_out), .out(multiplexer_1_out), .sel(in_8));
  Clock clock_1 (.out(clock_1_out));
  Register AC (.D(adder_1_out), .en(in_1), .Q(AC_q), .clk(clock_1_out), .clr(in_11));
  Register PC (.D(adder_1_out), .en(in_4), .Q(PC_q), .clk(clock_1_out), .clr(in_11));
  Register IR_Addr (.D(adder_1_out), .en(in_5), .Q(IR_Addr_q), .clk(clock_1_out), .clr(in_11));
  Register MBR (.D(multiplexer_1_out), .en(in_7), .Q(MBR_q), .clk(clock_1_out), .clr(in_11));
  Register MAR (.D(adder_1_out), .en(in_9), .Q(MAR_q), .clk(clock_1_out), .clr(in_11));
  assign controlled_buffer_1_out = not_1_out ? MBR_q : 8'bz;  // Controlled_Buffer controlled_buffer_1
  not not_1 (not_1_out, in_12);
  Multiplexer #(.select(2), .width(8), .enable("false")) multiplexer_2 (
    .in0(AC_q), .in1(PC_q), .in2(IR_Addr_q), .in3(MBR_q), .out(multiplexer_2_out), .sel(in_3));
  Multiplexer #(.select(2), .width(8), .enable("false")) multiplexer_3 (
    .in0(AC_q), .in1(PC_q), .in2(IR_Addr_q), .in3(MBR_q), .out(multiplexer_3_out), .sel(in_6));
  Register IR_Op (.D(MBR_q), .en(in_10), .clk(clock_1_out), .clr(in_11));  // open: Q
  Hex_Digit_Display hex_digit_display_1 (.value(adder_1_out[7:4]));  // open: dp
  Adder adder_1 (.a(multiplexer_2_out), .b(multiplexer_3_out), .out(adder_1_out), .cin(in_2));  // open: cout
  Hex_Digit_Display hex_digit_display_2 (.value(adder_1_out[3:0]));  // open: dp
  RAM ram_1 (.addr(MAR_q), .data(controlled_buffer_1_out), .sel(in_13), .clk(clock_1_out), .ld(in_12));  // open: clr
endmodule

module simple_data_path (
  input  in_1,
  input  in_2,
  input  [1:0] in_3,
  input  in_4,
  input  in_5,
  input  [1:0] in_6,
  input  in_7,
  input  in_8,
  input  in_9,
  input  in_10
);

  wire clock_1_out;
  wire [7:0] AC_q, adder_1_out, IR_Addr_q, MBR_q, multiplexer_1_out, multiplexer_2_out, PC_q;

  Clock clock_1 (.out(clock_1_out));
  Register AC (.D(adder_1_out), .en(in_1), .Q(AC_q), .clk(clock_1_out), .clr(in_10));
  Register PC (.D(adder_1_out), .en(in_4), .Q(PC_q), .clk(clock_1_out), .clr(in_10));
  Register IR_Addr (.D(adder_1_out), .en(in_5), .Q(IR_Addr_q), .clk(clock_1_out), .clr(in_10));
  Register MBR (.D(adder_1_out), .en(in_7), .Q(MBR_q), .clk(clock_1_out), .clr(in_10));
  Register MAR (.D(adder_1_out), .en(in_8), .clk(clock_1_out), .clr(in_10));  // open: Q
  Multiplexer #(.select(2), .width(8), .enable("false")) multiplexer_1 (
    .in0(AC_q), .in1(PC_q), .in2(IR_Addr_q), .in3(MBR_q), .out(multiplexer_1_out), .sel(in_3));
  Multiplexer #(.select(2), .width(8), .enable("false")) multiplexer_2 (
    .in0(AC_q), .in1(PC_q), .in2(IR_Addr_q), .in3(MBR_q), .out(multiplexer_2_out), .sel(in_6));
  Register IR_Op (.D(MBR_q), .en(in_9), .clk(clock_1_out), .clr(in_10));  // open: Q
  Hex_Digit_Display hex_digit_display_1 (.value(adder_1_out[7:4]));  // open: dp
  Adder adder_1 (.a(multiplexer_1_out), .b(multiplexer_2_out), .out(adder_1_out), .cin(in_2));  // open: cout
  Hex_Digit_Display hex_digit_display_2 (.value(adder_1_out[3:0]));  // open: dp
endmodule

module _4register_ALU (
  input  in_1,
  input  in_2,
  input  [1:0] in_3,
  input  in_4,
  input  in_5,
  input  [1:0] in_6,
  input  in_7,
  input  in_8
);

  wire clock_1_out;
  wire [7:0] AC_q, adder_1_out, IR_Addr_q, MBR_q, multiplexer_1_out, multiplexer_2_out, PC_q;

  Clock clock_1 (.out(clock_1_out));
  Register AC (.D(adder_1_out), .en(in_1), .Q(AC_q), .clk(clock_1_out), .clr(in_8));
  Register PC (.D(adder_1_out), .en(in_4), .Q(PC_q), .clk(clock_1_out), .clr(in_8));
  Register IR_Addr (.D(adder_1_out), .en(in_5), .Q(IR_Addr_q), .clk(clock_1_out), .clr(in_8));
  Register MBR (.D(adder_1_out), .en(in_7), .Q(MBR_q), .clk(clock_1_out), .clr(in_8));
  Multiplexer #(.select(2), .width(8), .enable("false")) multiplexer_1 (
    .in0(AC_q), .in1(PC_q), .in2(IR_Addr_q), .in3(MBR_q), .out(multiplexer_1_out), .sel(in_3));
  Multiplexer #(.select(2), .width(8), .enable("false")) multiplexer_2 (
    .in0(AC_q), .in1(PC_q), .in2(IR_Addr_q), .in3(MBR_q), .out(multiplexer_2_out), .sel(in_6));
  Hex_Digit_Display hex_digit_display_1 (.value(adder_1_out[7:4]));  // open: dp
  Adder adder_1 (.a(multiplexer_1_out), .b(multiplexer_2_out), .out(adder_1_out), .cin(in_2));  // open: cout
  Hex_Digit_Display hex_digit_display_2 (.value(adder_1_out[3:0]));  // open: dp
endmodule

module _4_register_data_path (
  input  in_1,
  input  [1:0] in_2,
  input  in_3,
  input  in_4,
  input  in_5,
  input  in_6
);

  wire clock_1_out;
  wire [7:0] AC_q, IR_Addr_q, MBR_q, multiplexer_1_out, PC_q;

  Clock clock_1 (.out(clock_1_out));
  Register AC (.D(multiplexer_1_out), .en(in_1), .Q(AC_q), .clk(clock_1_out), .clr(in_6));
  Register PC (.D(multiplexer_1_out), .en(in_3), .Q(PC_q), .clk(clock_1_out), .clr(in_6));
  Register IR_Addr (.D(multiplexer_1_out), .en(in_4), .Q(IR_Addr_q), .clk(clock_1_out), .clr(in_6));
  Register MBR (.D(multiplexer_1_out), .en(in_5), .Q(MBR_q), .clk(clock_1_out), .clr(in_6));
  Multiplexer #(.select(2), .width(8), .enable("false")) multiplexer_1 (
    .in0(AC_q), .in1(PC_q), .in2(IR_Addr_q), .in3(MBR_q), .out(multiplexer_1_out), .sel(in_2));
  Hex_Digit_Display hex_digit_display_1 (.value(multiplexer_1_out[7:4]));  // open: dp
  Hex_Digit_Display hex_digit_display_2 (.value(multiplexer_1_out[3:0]));  // open: dp
endmodule
