// Logisim project decoder_mux.circ as structural Verilog: 7 circuits, main circuit main
module main (
  input  in_1,
  input  in_2,
  input  in_3,
  input  in_4,
  input  in_5,
  input  in_6,
  output out_7,
  output out_8,
  output out_9,
  output out_10
);

  wire n4x1_mux_1_o;

  _4x1_mux u_4x1_mux_1 (.S1(in_6), .S0(in_5), .I0(in_1), .I1(in_2), .I2(in_3), .I3(in_4), .O(n4x1_mux_1_o));
  _1x4_demux u_1x4_demux_1 (.C1(in_6), .C0(in_5), .E(n4x1_mux_1_o), .D0(out_7), .D1(out_8), .D2(out_9), .D3(out_10));
endmodule

module _1x2_decoder (
  input  C0,
  output D0,
  output D1
);

  not not_1 (D0, C0);

  assign D1 = C0;
endmodule

// 2x4
module _2x4_decoder (
  input  C1,
  input  C0,
  input  E,
  output D0,
  output D1,
  output D2,
  output D3
);

  wire not_1_out, not_2_out;

  not not_1 (not_1_out, C1);
  not not_2 (not_2_out, C0);
  and and_1 (D0, not_2_out, not_1_out, E);
  and and_2 (D1, C0, not_1_out, E);
  and and_3 (D2, not_2_out, C1, E);
  and and_4 (D3, C0, C1, E);
endmodule

// 3x8
module _3x8_decoder (
  input  C2,
  input  C1,
  input  C0,
  input  E,
  output out_5,
  output out_6,
  output out_7,
  output out_8,
  output out_9,
  output out_10,
  output out_11,
  output out_12
);

  wire not_1_out, not_2_out, not_3_out;

  not not_1 (not_1_out, C2);
  not not_2 (not_2_out, C1);
  not not_3 (not_3_out, C0);
  and and_1 (out_5, not_1_out, not_2_out, not_3_out, E);
  and and_2 (out_6, not_1_out, not_2_out, C0, E);
  and and_3 (out_7, not_1_out, C1, not_3_out, E);
  and and_4 (out_8, not_1_out, C1, C0, E);
  and and_5 (out_9, C2, not_2_out, not_3_out, E);
  and and_6 (out_10, C2, not_2_out, C0, E);
  and and_7 (out_11, C2, C1, not_3_out, E);
  and and_8 (out_12, C2, C1, C0, E);
endmodule

module _4x16_decoder (
  input  [3:0] C
);

  wire not_1_out;

  not not_1 (not_1_out, C[3]);
  _3x8_decoder u_3x8_decoder_1 (
    .C2(C[2]), .C1(C[1]), .C0(C[0]), .E(not_1_out));  // open: out_5, out_6, out_7, out_8, out_9, out_10, out_11, out_12
  _3x8_decoder u_3x8_decoder_2 (
    .C2(C[2]), .C1(C[1]), .C0(C[0]), .E(C[3]));  // open: out_5, out_6, out_7, out_8, out_9, out_10, out_11, out_12
endmodule

module _4x1_mux (
  input  S1,
  input  S0,
  input  I0,
  input  I1,
  input  I2,
  input  I3,
  output O
);

  wire and_1_out, and_2_out, and_3_out, and_4_out, not_1_out, not_2_out;

  not not_1 (not_1_out, S1);
  not not_2 (not_2_out, S0);
  and and_1 (and_1_out, not_2_out, not_1_out, I0);
  and and_2 (and_2_out, S0, not_1_out, I1);
  and and_3 (and_3_out, not_2_out, S1, I2);
  and and_4 (and_4_out, S0, S1, I3);
  or or_1 (O, and_1_out, and_2_out, and_3_out, and_4_out);
endmodule

module _1x4_demux (
  input  C1,
  input  C0,
  input  E,
  output D0,
  output D1,
  output D2,
  output D3
);

  wire not_1_out, not_2_out;

  not not_1 (not_1_out, C1);
  not not_2 (not_2_out, C0);
  and and_1 (D0, not_2_out, not_1_out, E);
  and and_2 (D1, C0, not_1_out, E);
  and and_3 (D2, not_2_out, C1, E);
  and and_4 (D3, C0, C1, E);
endmodule
