// Logisim project prob_1.circ as structural Verilog: 18 circuits, main circuit main
module main (
  input  in_1,
  input  in_2
);

  wire acld, clock_1_out, control_unit_1_p5, iraddrld, iropld, M, marld, mbrld, not_1_out, pcld, rw, stld;
  wire [1:0] A, B;
  wire [3:0] n8_alu_1_v, register_1_q;
  wire [5:0] ALU;
  wire [7:0] AC_q, controlled_buffer_1_out, IR_Addr_q, IR_Op_q, MAR_q, MBR_q, multiplexer_1_out,
       multiplexer_2_out, multiplexer_3_out, n8_alu_1_f, PC_q;

  Multiplexer #(.width(8)) multiplexer_1 (
    .in0(n8_alu_1_f), .in1(controlled_buffer_1_out), .out(multiplexer_1_out), .sel(M));  // open: en
  Clock clock_1 (.out(clock_1_out));
  Register AC (.D(n8_alu_1_f), .en(acld), .Q(AC_q), .clk(clock_1_out), .clr(in_1));
  Register PC (.D(n8_alu_1_f), .en(pcld), .Q(PC_q), .clk(clock_1_out), .clr(in_1));
  Register IR_Addr (.D(n8_alu_1_f), .en(iraddrld), .Q(IR_Addr_q), .clk(clock_1_out), .clr(in_1));
  Register MBR (.D(multiplexer_1_out), .en(mbrld), .Q(MBR_q), .clk(clock_1_out), .clr(in_1));
  Register MAR (.D(n8_alu_1_f), .en(marld), .Q(MAR_q), .clk(clock_1_out), .clr(in_1));
  assign controlled_buffer_1_out = not_1_out ? MBR_q : 8'bz;  // Controlled_Buffer controlled_buffer_1
  not not_1 (not_1_out, rw);
  Multiplexer #(.select(2), .width(8)) multiplexer_2 (
    .in0(AC_q), .in1(PC_q), .in2(IR_Addr_q), .in3(MBR_q), .out(multiplexer_2_out), .sel(A));  // open: en
  // Probe on multiplexer_2_out
  // Probe on multiplexer_3_out
  Multiplexer #(.select(2), .width(8)) multiplexer_3 (
    .in0(AC_q), .in1(PC_q), .in2(IR_Addr_q), .in3(MBR_q), .out(multiplexer_3_out), .sel(B));  // open: en
  Register IR_Op (.D(MBR_q), .en(iropld), .Q(IR_Op_q), .clk(clock_1_out), .clr(in_1));
  // Probe on n8_alu_1_f
  _8_ALU u_8_alu_1 (
    .A(multiplexer_2_out), .B(multiplexer_3_out), .in_3(ALU), .V(n8_alu_1_v[0]), .Co(n8_alu_1_v[1]),
    .Z(n8_alu_1_v[2]), .S(n8_alu_1_v[3]), .F(n8_alu_1_f));
  Register #(.width(4)) register_1 (.D(n8_alu_1_v), .en(stld), .Q(register_1_q), .clk(clock_1_out), .clr(in_1));
  // Probe on control_unit_1_p5
  // Control_Unit control_unit_1: pin names not known; wires that end beside it: register_1_q, IR_Op_q, clock_1_out, in_1, control_unit_1_p5, A, B, M, ALU, {acld, pcld, iraddrld, mbrld, marld, iropld, stld}, rw
  RAM ram_1 (.addr(MAR_q), .data(controlled_buffer_1_out), .sel(in_2), .clk(clock_1_out), .ld(rw));  // open: clr
endmodule

// 2x1 mux
module _2x1_MUX (
  input  S,
  input  I0,
  input  I1,
  output O
);

  wire and_1_out, and_2_out, not_1_out;

  not not_1 (not_1_out, S);
  and and_1 (and_1_out, not_1_out, I0);
  and and_2 (and_2_out, S, I1);
  or or_1 (O, and_1_out, and_2_out);
endmodule

// 4x1 mux
module _4x1_MUX (
  input  S1,
  input  S0,
  input  I0,
  input  I1,
  input  I2,
  input  I3,
  output out_7
);

  wire and_1_out, and_2_out, and_3_out, and_4_out, not_1_out, not_2_out;

  not not_1 (not_1_out, S1);
  not not_2 (not_2_out, S0);
  and and_1 (and_1_out, not_2_out, not_1_out, I0);
  and and_2 (and_2_out, S0, not_1_out, I1);
  and and_3 (and_3_out, not_2_out, S1, I2);
  and and_4 (and_4_out, S0, S1, I3);
  or or_1 (out_7, and_1_out, and_2_out, and_3_out, and_4_out);
endmodule

// 1LU
module _1bit_LU (
  input  A,
  input  B,
  input  S1,
  input  S0,
  output out_5
);

  wire and_1_out, not_1_out, or_1_out, xor_1_out;

  not not_1 (not_1_out, A);
  and and_1 (and_1_out, A, B);
  or or_1 (or_1_out, A, B);
  xor xor_1 (xor_1_out, A, B);
  _4x1_MUX u_4x1_mux_1 (.S1(S1), .S0(S0), .I0(and_1_out), .I1(or_1_out), .I2(xor_1_out), .I3(not_1_out), .out_7(out_5));
endmodule

// 4LU
module _4bit_LU (
  input  [3:0] A,
  input  [3:0] B,
  input  S1,
  input  S0,
  output [3:0] F
);

  _1bit_LU u_1bit_lu_1 (.A(A[0]), .B(B[0]), .S1(S1), .S0(S0), .out_5(F[0]));
  _1bit_LU u_1bit_lu_2 (.A(A[1]), .B(B[1]), .S1(S1), .S0(S0), .out_5(F[1]));
  _1bit_LU u_1bit_lu_3 (.A(A[2]), .B(B[2]), .S1(S1), .S0(S0), .out_5(F[2]));
  _1bit_LU u_1bit_lu_4 (.A(A[3]), .B(B[3]), .S1(S1), .S0(S0), .out_5(F[3]));
endmodule

// 4bit shif
module _4bit_shifter (
  input  SLin,
  input  [3:0] I,
  input  SRin,
  input  S1L,
  input  S0R,
  output [3:0] O
);

  _4x1_MUX u_4x1_mux_1 (.S1(S1L), .S0(S0R), .I0(I[0]), .I1(I[1]), .I2(SLin), .I3(1'b0), .out_7(O[0]));
  _4x1_MUX u_4x1_mux_2 (.S1(S1L), .S0(S0R), .I0(I[1]), .I1(I[2]), .I2(I[0]), .I3(1'b0), .out_7(O[1]));
  _4x1_MUX u_4x1_mux_3 (.S1(S1L), .S0(S0R), .I0(I[2]), .I1(I[3]), .I2(I[1]), .I3(1'b0), .out_7(O[2]));
  _4x1_MUX u_4x1_mux_4 (.S1(S1L), .S0(S0R), .I0(I[3]), .I1(SRin), .I2(I[2]), .I3(1'b0), .out_7(O[3]));
endmodule

// 8 LU
module _8bit_LU (
  input  [7:0] A,
  input  [7:0] B,
  input  S1,
  input  S0,
  output [7:0] out_5
);

  _4bit_LU u_4bit_lu_1 (.A(A[3:0]), .B(B[3:0]), .S1(S1), .S0(S0), .F(out_5[3:0]));
  _4bit_LU u_4bit_lu_2 (.A(A[7:4]), .B(B[7:4]), .S1(S1), .S0(S0), .F(out_5[7:4]));
endmodule

// 8 SH
module _8bit_shifter (
  input  SLin,
  input  [7:0] I,
  input  SRin,
  input  S1L,
  input  S0R,
  output [7:0] O
);

  _4x1_MUX u_4x1_mux_1 (.S1(S1L), .S0(S0R), .I0(I[0]), .I1(I[1]), .I2(SLin), .I3(1'b0), .out_7(O[0]));
  _4x1_MUX u_4x1_mux_2 (.S1(S1L), .S0(S0R), .I0(I[1]), .I1(I[2]), .I2(I[0]), .I3(1'b0), .out_7(O[1]));
  _4x1_MUX u_4x1_mux_3 (.S1(S1L), .S0(S0R), .I0(I[2]), .I1(I[3]), .I2(I[1]), .I3(1'b0), .out_7(O[2]));
  _4x1_MUX u_4x1_mux_4 (.S1(S1L), .S0(S0R), .I0(I[3]), .I1(I[4]), .I2(I[2]), .I3(1'b0), .out_7(O[3]));
  _4x1_MUX u_4x1_mux_5 (.S1(S1L), .S0(S0R), .I0(I[4]), .I1(I[5]), .I2(I[3]), .I3(1'b0), .out_7(O[4]));
  _4x1_MUX u_4x1_mux_6 (.S1(S1L), .S0(S0R), .I0(I[5]), .I1(I[6]), .I2(I[4]), .I3(1'b0), .out_7(O[5]));
  _4x1_MUX u_4x1_mux_7 (.S1(S1L), .S0(S0R), .I0(I[6]), .I1(I[7]), .I2(I[5]), .I3(1'b0), .out_7(O[6]));
  _4x1_MUX u_4x1_mux_8 (.S1(S1L), .S0(S0R), .I0(I[7]), .I1(SRin), .I2(I[6]), .I3(1'b0), .out_7(O[7]));
endmodule

// FA
module full_adder (
  input  A,
  input  B,
  input  Ci,
  output S,
  output Co
);

  wire and_1_out, and_2_out, and_3_out, and_4_out, and_5_out, and_6_out, and_7_out, not_1_out, not_2_out,
       not_3_out, not_4_out, not_5_out, not_6_out;

  not not_1 (not_1_out, A);
  not not_2 (not_2_out, B);
  not not_3 (not_3_out, A);
  not not_4 (not_4_out, Ci);
  not not_5 (not_5_out, B);
  not not_6 (not_6_out, Ci);
  and and_1 (and_1_out, not_1_out, not_2_out, Ci);
  and and_2 (and_2_out, not_3_out, B, not_4_out);
  and and_3 (and_3_out, A, not_5_out, not_6_out);
  and and_4 (and_4_out, A, B, Ci);
  and and_5 (and_5_out, B, Ci);
  and and_6 (and_6_out, A, Ci);
  or or_1 (Co, and_5_out, and_6_out, and_7_out);
  and and_7 (and_7_out, A, B);
  or or_2 (S, and_1_out, and_2_out, and_3_out, and_4_out);
endmodule

// 1 AU
module _1bit_AU (
  input  Ci,
  input  A,
  input  B,
  input  S1,
  input  S0,
  output F,
  output Co
);

  wire n4x1_mux_1_out_7, not_1_out;

  not not_1 (not_1_out, B);
  _4x1_MUX u_4x1_mux_1 (.S1(S1), .S0(S0), .I0(1'b0), .I1(B), .I2(not_1_out), .I3(1'b1), .out_7(n4x1_mux_1_out_7));
  full_adder full_adder_1 (.A(A), .B(n4x1_mux_1_out_7), .Ci(Ci), .S(F), .Co(Co));
endmodule

// 4 AU
module _4bit_AU (
  input  Ci,
  input  [3:0] A,
  input  [3:0] B,
  input  S1,
  input  S0,
  output [3:0] F,
  output V,
  output out_8
);

  wire n1bit_au_1_co, n1bit_au_2_co, n1bit_au_3_co;

  _1bit_AU u_1bit_au_1 (.Ci(Ci), .A(A[0]), .B(B[0]), .S1(S1), .S0(S0), .F(F[0]), .Co(n1bit_au_1_co));
  _1bit_AU u_1bit_au_2 (.Ci(n1bit_au_1_co), .A(A[1]), .B(B[1]), .S1(S1), .S0(S0), .F(F[1]), .Co(n1bit_au_2_co));
  _1bit_AU u_1bit_au_3 (.Ci(n1bit_au_2_co), .A(A[2]), .B(B[2]), .S1(S1), .S0(S0), .F(F[2]), .Co(n1bit_au_3_co));
  _1bit_AU u_1bit_au_4 (.Ci(n1bit_au_3_co), .A(A[3]), .B(B[3]), .S1(S1), .S0(S0), .F(F[3]), .Co(out_8));
  xor xor_1 (V, n1bit_au_3_co, out_8);
endmodule

// 4 2x1
module _4bit_2x1_MUX (
  input  [3:0] A,
  input  [3:0] B,
  input  S,
  output [3:0] out_4
);

  _2x1_MUX u_2x1_mux_1 (.S(S), .I0(A[0]), .I1(B[0]), .O(out_4[0]));
  _2x1_MUX u_2x1_mux_2 (.S(S), .I0(A[1]), .I1(B[1]), .O(out_4[1]));
  _2x1_MUX u_2x1_mux_3 (.S(S), .I0(A[2]), .I1(B[2]), .O(out_4[2]));
  _2x1_MUX u_2x1_mux_4 (.S(S), .I0(A[3]), .I1(B[3]), .O(out_4[3]));
endmodule

module _4bit_ALU (
  input  [3:0] A,
  input  [3:0] B,
  input  H1,
  input  H0,
  input  S2,
  input  S1,
  input  S0,
  input  Ci,
  output V,
  output Co,
  output Z,
  output S,
  output [3:0] out_13
);

  wire [3:0] n4bit_2x1_mux_1_out_4, n4bit_au_1_f, n4bit_lu_1_f;

  _4bit_AU u_4bit_au_1 (.Ci(Ci), .A(A), .B(B), .S1(S1), .S0(S0), .F(n4bit_au_1_f), .V(V), .out_8(Co));
  _4bit_LU u_4bit_lu_1 (.A(A), .B(B), .S1(S1), .S0(S0), .F(n4bit_lu_1_f));
  _4bit_2x1_MUX u_4bit_2x1_mux_1 (.A(n4bit_au_1_f), .B(n4bit_lu_1_f), .S(S2), .out_4(n4bit_2x1_mux_1_out_4));
  _4bit_shifter u_4bit_shifter_1 (.SLin(1'b0), .I(n4bit_2x1_mux_1_out_4), .SRin(1'b0), .S1L(H1), .S0R(H0), .O(out_13));
  nor nor_1 (Z, out_13[0], out_13[1], out_13[2], out_13[3]);

  assign S = out_13[3];
endmodule

// 8 2x1
module _8bit_2x1_MUX (
  input  [7:0] A,
  input  [7:0] B,
  input  S,
  output [7:0] out_4
);

  _2x1_MUX u_2x1_mux_1 (.S(S), .I0(A[0]), .I1(B[0]), .O(out_4[0]));
  _2x1_MUX u_2x1_mux_2 (.S(S), .I0(A[1]), .I1(B[1]), .O(out_4[1]));
  _2x1_MUX u_2x1_mux_3 (.S(S), .I0(A[2]), .I1(B[2]), .O(out_4[2]));
  _2x1_MUX u_2x1_mux_4 (.S(S), .I0(A[3]), .I1(B[3]), .O(out_4[3]));
  _2x1_MUX u_2x1_mux_5 (.S(S), .I0(A[4]), .I1(B[4]), .O(out_4[4]));
  _2x1_MUX u_2x1_mux_6 (.S(S), .I0(A[5]), .I1(B[5]), .O(out_4[5]));
  _2x1_MUX u_2x1_mux_7 (.S(S), .I0(A[6]), .I1(B[6]), .O(out_4[6]));
  _2x1_MUX u_2x1_mux_8 (.S(S), .I0(A[7]), .I1(B[7]), .O(out_4[7]));
endmodule

// 8 AU
module _8bit_AU (
  input  Ci,
  input  [7:0] A,
  input  [7:0] B,
  input  S1,
  input  S0,
  output [7:0] F,
  output V,
  output Co
);

  wire n1bit_au_1_co, n1bit_au_2_co, n1bit_au_3_co, n1bit_au_4_co, n1bit_au_5_co, n1bit_au_6_co,
       n1bit_au_7_co;

  _1bit_AU u_1bit_au_1 (.Ci(Ci), .A(A[0]), .B(B[0]), .S1(S1), .S0(S0), .F(F[0]), .Co(n1bit_au_1_co));
  _1bit_AU u_1bit_au_2 (.Ci(n1bit_au_1_co), .A(A[1]), .B(B[1]), .S1(S1), .S0(S0), .F(F[1]), .Co(n1bit_au_2_co));
  _1bit_AU u_1bit_au_3 (.Ci(n1bit_au_2_co), .A(A[2]), .B(B[2]), .S1(S1), .S0(S0), .F(F[2]), .Co(n1bit_au_3_co));
  _1bit_AU u_1bit_au_4 (.Ci(n1bit_au_3_co), .A(A[3]), .B(B[3]), .S1(S1), .S0(S0), .F(F[3]), .Co(n1bit_au_4_co));
  _1bit_AU u_1bit_au_5 (.Ci(n1bit_au_4_co), .A(A[4]), .B(B[4]), .S1(S1), .S0(S0), .F(F[4]), .Co(n1bit_au_5_co));
  _1bit_AU u_1bit_au_6 (.Ci(n1bit_au_5_co), .A(A[5]), .B(B[5]), .S1(S1), .S0(S0), .F(F[5]), .Co(n1bit_au_6_co));
  _1bit_AU u_1bit_au_7 (.Ci(n1bit_au_6_co), .A(A[6]), .B(B[6]), .S1(S1), .S0(S0), .F(F[6]), .Co(n1bit_au_7_co));
  _1bit_AU u_1bit_au_8 (.Ci(n1bit_au_7_co), .A(A[7]), .B(B[7]), .S1(S1), .S0(S0), .F(F[7]), .Co(Co));
  xor xor_1 (V, n1bit_au_7_co, Co);
endmodule

module _8bit_ALU (
  input  [7:0] A,
  input  [7:0] B,
  input  S2,
  input  S1,
  input  H1,
  input  S0,
  input  H0,
  input  Ci,
  output V,
  output Co,
  output Z,
  output S,
  output [7:0] F
);

  wire [7:0] n8bit_2x1_mux_1_out_4, n8bit_au_1_f, n8bit_lu_1_out_5;

  _8bit_AU u_8bit_au_1 (.Ci(Ci), .A(A), .B(B), .S1(S1), .S0(S0), .F(n8bit_au_1_f), .V(V), .Co(Co));
  _8bit_LU u_8bit_lu_1 (.A(A), .B(B), .S1(S1), .S0(S0), .out_5(n8bit_lu_1_out_5));
  _8bit_2x1_MUX u_8bit_2x1_mux_1 (.A(n8bit_au_1_f), .B(n8bit_lu_1_out_5), .S(S2), .out_4(n8bit_2x1_mux_1_out_4));
  _8bit_shifter u_8bit_shifter_1 (.SLin(1'b0), .I(n8bit_2x1_mux_1_out_4), .SRin(1'b0), .S1L(H1), .S0R(H0), .O(F));
  nor nor_1 (Z, F[0], F[1], F[2], F[3], F[4], F[5], F[6], F[7]);

  assign S = F[7];
endmodule

module _8_ALU (
  input  [7:0] A,
  input  [7:0] B,
  input  [5:0] in_3,
  output V,
  output Co,
  output Z,
  output S,
  output [7:0] F
);

  wire [7:0] n8bit_2x1_mux_1_out_4, n8bit_au_1_f, n8bit_lu_1_out_5;

  _8bit_AU u_8bit_au_1 (.Ci(in_3[2]), .A(A), .B(B), .S1(in_3[4]), .S0(in_3[3]), .F(n8bit_au_1_f), .V(V), .Co(Co));
  _8bit_LU u_8bit_lu_1 (.A(A), .B(B), .S1(in_3[4]), .S0(in_3[3]), .out_5(n8bit_lu_1_out_5));
  _8bit_2x1_MUX u_8bit_2x1_mux_1 (.A(n8bit_au_1_f), .B(n8bit_lu_1_out_5), .S(in_3[5]), .out_4(n8bit_2x1_mux_1_out_4));
  _8bit_shifter u_8bit_shifter_1 (
    .SLin(1'b0), .I(n8bit_2x1_mux_1_out_4), .SRin(1'b0), .S1L(in_3[0]), .S0R(in_3[1]), .O(F));
  nor nor_1 (Z, F[0], F[1], F[2], F[3], F[4], F[5], F[6], F[7]);

  assign S = F[7];
endmodule

// CU7
module Control_Unit (
  input  Ck,
  input  Reset,
  input  [3:0] st,
  input  [7:0] IR_Op,
  output M,
  output [1:0] A,
  output [1:0] B,
  output rw,
  output [2:0] counter,
  output [5:0] ALU,
  output [6:0] LDs
);

  wire AC2BR, ADD, ADD_T4, ADD_T5, AND, BR2AC, BZ, IRAD2AR, IRAD2PC, JMP, LDA, LDA_T4, LDA_T5, NOP, NOT,
       not_1_out, OR, READ, SHL, SHR, STR, STR_T4, STR_T6, SUB, T0, T1, T4, T5, T6, T7, XOR;

  Counter #(.width(3), .max('h7)) counter_1 (.Q(counter), .clk(not_1_out), .clr(Reset));  // open: load, D, count, carry
  not not_1 (not_1_out, Ck);
  Decoder #(.select(3), .disabled(0), .enable("false")) decoder_1 (
    .out0(T0), .out1(T1), .out2(LDs[1]), .out3(LDs[4]), .out4(T4), .out5(T5), .out6(T6), .out7(T7),
    .sel(counter));
  Decoder #(.select(4), .disabled(0), .enable("false")) decoder_2 (
    .out0(NOP), .out1(NOT), .out2(SHL), .out3(SHR), .out4(JMP), .out5(BZ), .out8(LDA), .out9(ADD),
    .out10(SUB), .out11(AND), .out12(OR), .out13(XOR), .out15(STR), .sel(IR_Op[7:4]));  // open: out6, out7, out14
  and and_1 (LDA_T4, LDA, T4);
  and and_2 (LDA_T5, LDA, T5);
  and and_3 (BR2AC, LDA, T6);
  and and_4 (ADD_T4, ADD, T4);
  and and_5 (ADD_T5, ADD, T5);
  and and_6 (ALU[3], ADD, T6);
  and and_7 (STR_T4, STR, T4);
  and and_8 (AC2BR, STR, T5);
  and and_9 (STR_T6, STR, T6);
  and and_10 (IRAD2PC, JMP, T4);
  or or_1 (IRAD2AR, LDA_T4, ADD_T4, STR_T4);
  or or_2 (READ, LDA_T5, ADD_T5);
  or or_3 (A[0], T0, T1, LDs[1], LDs[4], BR2AC);
  or or_4 (A[1], LDs[4], IRAD2AR, IRAD2PC, BR2AC);
  or or_5 (LDs[6], BR2AC, ALU[3]);
  or or_6 (LDs[2], T0, IRAD2AR, T1);
  or or_7 (LDs[3], T1, READ, AC2BR, LDs[1]);
  or or_8 (LDs[5], T1, IRAD2PC, LDs[1]);
  or or_9 (ALU[2], T1, LDs[1]);
  or or_10 (M, T1, READ, LDs[1]);
  not not_2 (rw, STR_T6);

  assign {ALU[5:4], ALU[1:0]} = 4'b0000;
  assign B = {2{ALU[3]}};
  assign LDs[0] = LDs[6];

  // Other names for the same wires on the sheet: ADD_T6 = ALU[3]; uADD = ALU[3]; JMP_T4 = IRAD2PC; LDA_T6 = BR2AC;
  //   T2 = LDs[1]; T3 = LDs[4]; V = st[0]; C = st[1]; Z = st[2]; S = st[3]; STR_T5 = AC2BR; WRITE = STR_T6
endmodule
