// Logisim project prob_2.circ as structural Verilog
// 2x1 mux
module _2x1_MUX (
  input  S,
  input  I0,
  input  I1,
  output O
);

  wire and_1_out, and_2_out, not_1_out;

  not not_1 (not_1_out, S);
  and and_1 (and_1_out, not_1_out, I0);
  and and_2 (and_2_out, S, I1);
  or or_1 (O, and_1_out, and_2_out);
endmodule

// 4X1 mux
module _4X1_MUX (
  input  S1,
  input  S0,
  input  I0,
  input  I1,
  input  I2,
  input  I3,
  output out_7
);

  wire and_1_out, and_2_out, and_3_out, and_4_out, not_1_out, not_2_out;

  not not_1 (not_1_out, S1);
  not not_2 (not_2_out, S0);
  and and_1 (and_1_out, not_2_out, not_1_out, I0);
  and and_2 (and_2_out, S0, I1, not_1_out);
  and and_3 (and_3_out, not_2_out, S1, I2);
  and and_4 (and_4_out, S0, S1, I3);
  or or_1 (out_7, and_1_out, and_2_out, and_3_out, and_4_out);
endmodule

// 1 LU
module _1bit_LU (
  input  A,
  input  B,
  input  S1,
  input  S0,
  output out_5
);

  wire and_1_out, not_1_out, or_1_out, xor_1_out;

  and and_1 (and_1_out, A, B);
  or or_1 (or_1_out, A, B);
  xor xor_1 (xor_1_out, A, B);
  not not_1 (not_1_out, A);
  _4X1_MUX u_4x1_mux_1 (.S1(S1), .S0(S0), .I0(and_1_out), .I1(or_1_out), .I2(xor_1_out), .I3(not_1_out), .out_7(out_5));
endmodule

// 4 LU
module _4bit_LU (
  input  [3:0] A,
  input  [3:0] B,
  input  S1,
  input  S0,
  output [3:0] F
);

  _1bit_LU u_1bit_lu_1 (.A(A[0]), .B(B[0]), .S1(S1), .S0(S0), .out_5(F[0]));
  _1bit_LU u_1bit_lu_2 (.A(A[1]), .B(B[1]), .S1(S1), .S0(S0), .out_5(F[1]));
  _1bit_LU u_1bit_lu_3 (.A(A[2]), .B(B[2]), .S1(S1), .S0(S0), .out_5(F[2]));
  _1bit_LU u_1bit_lu_4 (.A(A[3]), .B(B[3]), .S1(S1), .S0(S0), .out_5(F[3]));
endmodule

// 4 shifter
module _4bit_shifter (
  input  SLin,
  input  [3:0] I,
  input  SRin,
  input  S1,
  input  S0,
  output [3:0] O
);

  _4X1_MUX u_4x1_mux_1 (.S1(S1), .S0(S0), .I0(I[0]), .I1(I[1]), .I2(SLin), .I3(1'b0), .out_7(O[0]));
  _4X1_MUX u_4x1_mux_2 (.S1(S1), .S0(S0), .I0(I[1]), .I1(I[2]), .I2(I[0]), .I3(1'b0), .out_7(O[1]));
  _4X1_MUX u_4x1_mux_3 (.S1(S1), .S0(S0), .I0(I[2]), .I1(I[3]), .I2(I[1]), .I3(1'b0), .out_7(O[2]));
  _4X1_MUX u_4x1_mux_4 (.S1(S1), .S0(S0), .I0(I[3]), .I1(SRin), .I2(I[2]), .I3(1'b0), .out_7(O[3]));
endmodule

// 8 LU
module _8bit_LU (
  input  [7:0] A,
  input  [7:0] B,
  input  S1,
  input  S2,
  output [7:0] O
);

  _4bit_LU u_4bit_lu_1 (.A(A[3:0]), .B(B[3:0]), .S1(S1), .S0(S2), .F(O[3:0]));
  _4bit_LU u_4bit_lu_2 (.A(A[7:4]), .B(B[7:4]), .S1(S1), .S0(S2), .F(O[7:4]));
endmodule

// 8 SH
module _8bit_shifter (
  input  SLin,
  input  [7:0] in_2,
  input  RLin,
  input  S1,
  input  S0,
  output [7:0] out_6
);

  _4X1_MUX u_4x1_mux_1 (.S1(S1), .S0(S0), .I0(in_2[0]), .I1(in_2[1]), .I2(SLin), .I3(1'b0), .out_7(out_6[0]));
  _4X1_MUX u_4x1_mux_2 (.S1(S1), .S0(S0), .I0(in_2[1]), .I1(in_2[2]), .I2(in_2[0]), .I3(1'b0), .out_7(out_6[1]));
  _4X1_MUX u_4x1_mux_3 (.S1(S1), .S0(S0), .I0(in_2[2]), .I1(in_2[3]), .I2(in_2[1]), .I3(1'b0), .out_7(out_6[2]));
  _4X1_MUX u_4x1_mux_4 (.S1(S1), .S0(S0), .I0(in_2[3]), .I1(in_2[4]), .I2(in_2[2]), .I3(1'b0), .out_7(out_6[3]));
  _4X1_MUX u_4x1_mux_5 (.S1(S1), .S0(S0), .I0(in_2[4]), .I1(in_2[5]), .I2(in_2[3]), .I3(1'b0), .out_7(out_6[4]));
  _4X1_MUX u_4x1_mux_6 (.S1(S1), .S0(S0), .I0(in_2[5]), .I1(in_2[6]), .I2(in_2[4]), .I3(1'b0), .out_7(out_6[5]));
  _4X1_MUX u_4x1_mux_7 (.S1(S1), .S0(S0), .I0(in_2[6]), .I1(in_2[7]), .I2(in_2[5]), .I3(1'b0), .out_7(out_6[6]));
  _4X1_MUX u_4x1_mux_8 (.S1(S1), .S0(S0), .I0(in_2[7]), .I1(RLin), .I2(in_2[6]), .I3(1'b0), .out_7(out_6[7]));
endmodule

// FA
module full_adder (
  input  A,
  input  B,
  input  Cin,
  output out_4,
  output out_5
);

  wire half_adder_1_c, half_adder_1_s, half_adder_2_c;

  half_adder half_adder_1 (.A(A), .B(B), .S(half_adder_1_s), .C(half_adder_1_c));
  half_adder half_adder_2 (.A(half_adder_1_s), .B(Cin), .S(out_4), .C(half_adder_2_c));
  or or_1 (out_5, half_adder_2_c, half_adder_1_c);
endmodule

// HA
module half_adder (
  input  A,
  input  B,
  output S,
  output C
);

  xor xor_1 (S, A, B);
  and and_1 (C, A, B);
endmodule

// 1 AU
module _1bit_AU (
  input  Cin,
  input  A,
  input  B,
  input  S1,
  input  S2,
  output F,
  output Co
);

  wire n4x1_mux_1_out_7, not_1_out;

  not not_1 (not_1_out, B);
  _4X1_MUX u_4x1_mux_1 (.S1(S1), .S0(S2), .I0(1'b0), .I1(B), .I2(not_1_out), .I3(1'b1), .out_7(n4x1_mux_1_out_7));
  full_adder full_adder_1 (.A(A), .B(n4x1_mux_1_out_7), .Cin(Cin), .out_4(F), .out_5(Co));
endmodule

// 4 AU
module _4bit_AU (
  input  Ci,
  input  [3:0] A,
  input  [3:0] B,
  input  S1,
  input  S0,
  output [3:0] F,
  output V,
  output Co
);

  wire n1bit_au_1_co, n1bit_au_2_co, n1bit_au_3_co;

  _1bit_AU u_1bit_au_1 (.Cin(Ci), .A(A[0]), .B(B[0]), .S1(S1), .S2(S0), .F(F[0]), .Co(n1bit_au_1_co));
  _1bit_AU u_1bit_au_2 (.Cin(n1bit_au_1_co), .A(A[1]), .B(B[1]), .S1(S1), .S2(S0), .F(F[1]), .Co(n1bit_au_2_co));
  _1bit_AU u_1bit_au_3 (.Cin(n1bit_au_2_co), .A(A[2]), .B(B[2]), .S1(S1), .S2(S0), .F(F[2]), .Co(n1bit_au_3_co));
  _1bit_AU u_1bit_au_4 (.Cin(n1bit_au_3_co), .A(A[3]), .B(B[3]), .S1(S1), .S2(S0), .F(F[3]), .Co(Co));
  xor xor_1 (V, n1bit_au_3_co, Co);
endmodule

// 4 2x1
module _4bit_2x1_MUX (
  input  [3:0] A,
  input  [3:0] B,
  input  S,
  output [3:0] O
);

  _2x1_MUX u_2x1_mux_1 (.S(S), .I0(A[0]), .I1(B[0]), .O(O[0]));
  _2x1_MUX u_2x1_mux_2 (.S(S), .I0(A[1]), .I1(B[1]), .O(O[1]));
  _2x1_MUX u_2x1_mux_3 (.S(S), .I0(A[2]), .I1(B[2]), .O(O[2]));
  _2x1_MUX u_2x1_mux_4 (.S(S), .I0(A[3]), .I1(B[3]), .O(O[3]));
endmodule

module _4bit_ALU (
  input  [3:0] A,
  input  [3:0] B,
  input  S2,
  input  S1,
  input  H1,
  input  S0,
  input  H0,
  input  Ci,
  output V,
  output Co,
  output Z,
  output S,
  output [3:0] F
);

  wire [3:0] n4bit_2x1_mux_1_o, n4bit_au_1_f, n4bit_lu_1_f;

  _4bit_AU u_4bit_au_1 (.A(A), .Ci(Ci), .F(n4bit_au_1_f), .S1(S1), .S0(S0), .V(V), .Co(Co));  // open: B
  _4bit_LU u_4bit_lu_1 (.B(B), .S1(S1), .S0(S0), .F(n4bit_lu_1_f));  // open: A
  _4bit_2x1_MUX u_4bit_2x1_mux_1 (.A(n4bit_au_1_f), .B(n4bit_lu_1_f), .S(S2), .O(n4bit_2x1_mux_1_o));
  _4bit_shifter u_4bit_shifter_1 (.SLin(1'b0), .I(n4bit_2x1_mux_1_o), .SRin(1'b0), .S1(H1), .S0(H0), .O(F));
  nor nor_1 (Z, F[0], F[1], F[2], F[3]);

  assign S = F[3];
endmodule

// 8 AU
module _8bit_AU (
  input  Ci,
  input  [7:0] A,
  input  [7:0] B,
  input  S1,
  input  S0,
  output [7:0] F,
  output V,
  output Co
);

  wire n1bit_au_1_co, n1bit_au_2_co, n1bit_au_3_co, n1bit_au_4_co, n1bit_au_5_co, n1bit_au_6_co,
       n1bit_au_7_co;

  _1bit_AU u_1bit_au_1 (.Cin(Ci), .A(A[0]), .B(B[0]), .S1(S1), .S2(S0), .F(F[0]), .Co(n1bit_au_1_co));
  _1bit_AU u_1bit_au_2 (.Cin(n1bit_au_1_co), .A(A[1]), .B(B[1]), .S1(S1), .S2(S0), .F(F[1]), .Co(n1bit_au_2_co));
  _1bit_AU u_1bit_au_3 (.Cin(n1bit_au_2_co), .A(A[2]), .B(B[2]), .S1(S1), .S2(S0), .F(F[2]), .Co(n1bit_au_3_co));
  _1bit_AU u_1bit_au_4 (.Cin(n1bit_au_3_co), .A(A[3]), .B(B[3]), .S1(S1), .S2(S0), .F(F[3]), .Co(n1bit_au_4_co));
  _1bit_AU u_1bit_au_5 (.Cin(n1bit_au_4_co), .A(A[4]), .B(B[4]), .S1(S1), .S2(S0), .F(F[4]), .Co(n1bit_au_5_co));
  _1bit_AU u_1bit_au_6 (.Cin(n1bit_au_5_co), .A(A[5]), .B(B[5]), .S1(S1), .S2(S0), .F(F[5]), .Co(n1bit_au_6_co));
  _1bit_AU u_1bit_au_7 (.Cin(n1bit_au_6_co), .A(A[6]), .B(B[6]), .S1(S1), .S2(S0), .F(F[6]), .Co(n1bit_au_7_co));
  _1bit_AU u_1bit_au_8 (.Cin(n1bit_au_7_co), .A(A[7]), .B(B[7]), .S1(S1), .S2(S0), .F(F[7]), .Co(Co));
  nor nor_1 (V, n1bit_au_7_co, Co);
endmodule

// 8 2x1
module _8bit_2x1_MUX (
  input  [7:0] A,
  input  [7:0] B,
  input  in_3,
  output [7:0] O
);

  _4bit_2x1_MUX u_4bit_2x1_mux_1 (.A(A[3:0]), .B(B[3:0]), .S(in_3), .O(O[3:0]));
  _4bit_2x1_MUX u_4bit_2x1_mux_2 (.A(A[7:4]), .B(B[7:4]), .S(in_3), .O(O[7:4]));
endmodule

// 8 ALU
module _8bit_ALU (
  input  [7:0] A,
  input  [7:0] B,
  input  [5:0] ALU,
  output V,
  output Co,
  output Z,
  output S,
  output [7:0] F
);

  wire [7:0] n8bit_2x1_mux_1_o, n8bit_au_1_f, n8bit_lu_1_o;

  _8bit_AU u_8bit_au_1 (.Ci(ALU[2]), .A(A), .B(B), .S1(ALU[4]), .S0(ALU[3]), .F(n8bit_au_1_f), .V(V), .Co(Co));
  _8bit_LU u_8bit_lu_1 (.A(A), .B(B), .S1(ALU[4]), .S2(ALU[3]), .O(n8bit_lu_1_o));
  _8bit_2x1_MUX u_8bit_2x1_mux_1 (.A(n8bit_au_1_f), .B(n8bit_lu_1_o), .in_3(ALU[5]), .O(n8bit_2x1_mux_1_o));
  _8bit_shifter u_8bit_shifter_1 (
    .SLin(1'b0), .in_2(n8bit_2x1_mux_1_o), .RLin(1'b0), .S1(ALU[1]), .S0(ALU[0]), .out_6(F));
  nor nor_1 (Z, F[0], F[1], F[2], F[3], F[4], F[5], F[6], F[7]);

  assign S = F[7];
endmodule

module \숙제6  (
  input  acld,
  input  [1:0] A,
  input  pcld,
  input  iraddrld,
  input  [5:0] ALU,
  input  [1:0] B,
  input  mbrld,
  input  M,
  input  marld,
  input  iropld,
  input  in_11,
  input  rw,
  input  in_13
);

  wire clock_1_out, not_1_out;
  wire [7:0] AC_q, controlled_buffer_1_out, IR_Addr_q, MAR_q, MBR_q, multiplexer_1_out, multiplexer_2_out,
       multiplexer_3_out, n8bit_alu_1_f, PC_q;

  Multiplexer #(.width(8), .enable("false")) multiplexer_1 (
    .in1(controlled_buffer_1_out), .out(multiplexer_1_out), .sel(M));  // open: in0
  Register AC (.D(n8bit_alu_1_f), .en(acld), .Q(AC_q), .clk(clock_1_out), .clr(in_11));
  Register PC (.D(n8bit_alu_1_f), .en(pcld), .Q(PC_q), .clk(clock_1_out), .clr(in_11));
  Register IR_Addr (.D(n8bit_alu_1_f), .en(iraddrld), .Q(IR_Addr_q), .clk(clock_1_out), .clr(in_11));
  Register MBR (.D(multiplexer_1_out), .en(mbrld), .Q(MBR_q), .clk(clock_1_out), .clr(in_11));
  Register MAR (.D(n8bit_alu_1_f), .en(marld), .Q(MAR_q), .clk(clock_1_out), .clr(in_11));
  Clock clock_1 (.out(clock_1_out));
  not not_1 (not_1_out, rw);
  assign controlled_buffer_1_out = not_1_out ? MBR_q : 8'bz;  // Controlled_Buffer controlled_buffer_1
  Multiplexer #(.select(2), .width(8), .enable("false")) multiplexer_2 (
    .in0(AC_q), .in1(PC_q), .in2(IR_Addr_q), .in3(MBR_q), .out(multiplexer_2_out), .sel(A));
  // Probe on multiplexer_2_out
  Multiplexer #(.select(2), .width(8), .enable("false")) multiplexer_3 (
    .in0(AC_q), .in1(PC_q), .in2(IR_Addr_q), .in3(MBR_q), .out(multiplexer_3_out), .sel(B));
  // Probe on multiplexer_3_out
  Register IR_Op (.D(MBR_q), .en(iropld), .clk(clock_1_out), .clr(in_11));  // open: Q
  _8bit_ALU u_8bit_alu_1 (
    .A(multiplexer_2_out), .B(multiplexer_3_out), .F(n8bit_alu_1_f), .ALU(ALU));  // open: V, Co, Z, S
  // Probe on n8bit_alu_1_f
  RAM ram_1 (.addr(MAR_q), .data(controlled_buffer_1_out), .sel(in_13), .clk(clock_1_out), .ld(rw));  // open: clr
endmodule

module \숙제8  (
  input  in_1,
  input  in_2
);

  wire acld, clock_1_out, iraddrld, iropld, M, marld, mbrld, not_1_out, pcld, rw, stld;
  wire [1:0] A, B;
  wire [2:0] add_lda_str_jmp_1_cnt;
  wire [3:0] n8bit_alu_1_v, status_q;
  wire [5:0] ALU;
  wire [7:0] AC_q, controlled_buffer_1_out, IR_Addr_q, IR_Op_q, MAR_q, MBR_q, multiplexer_1_out,
       multiplexer_2_out, multiplexer_3_out, n8bit_alu_1_f, PC_q;

  Multiplexer #(.width(8), .enable("false")) multiplexer_1 (
    .in1(controlled_buffer_1_out), .out(multiplexer_1_out), .sel(M));  // open: in0
  // Probe on M
  Register AC (.D(n8bit_alu_1_f), .en(acld), .Q(AC_q), .clk(clock_1_out), .clr(in_1));
  Register PC (.D(n8bit_alu_1_f), .en(pcld), .Q(PC_q), .clk(clock_1_out), .clr(in_1));
  Register IR_Addr (.D(n8bit_alu_1_f), .en(iraddrld), .Q(IR_Addr_q), .clk(clock_1_out), .clr(in_1));
  Register MBR (.D(multiplexer_1_out), .en(mbrld), .Q(MBR_q), .clk(clock_1_out), .clr(in_1));
  Register MAR (.D(n8bit_alu_1_f), .en(marld), .Q(MAR_q), .clk(clock_1_out), .clr(in_1));
  Clock clock_1 (.out(clock_1_out));
  not not_1 (not_1_out, rw);
  assign controlled_buffer_1_out = not_1_out ? MBR_q : 8'bz;  // Controlled_Buffer controlled_buffer_1
  Multiplexer #(.select(2), .width(8), .enable("false")) multiplexer_2 (
    .in0(AC_q), .in1(PC_q), .in2(IR_Addr_q), .in3(MBR_q), .out(multiplexer_2_out), .sel(A));
  // Probe on multiplexer_2_out
  Multiplexer #(.select(2), .width(8), .enable("false")) multiplexer_3 (
    .in0(AC_q), .in1(PC_q), .in2(IR_Addr_q), .in3(MBR_q), .out(multiplexer_3_out), .sel(B));
  // Probe on ALU
  // Probe on multiplexer_3_out
  Register #(.width(4)) status (.D(n8bit_alu_1_v), .en(stld), .Q(status_q), .clk(clock_1_out), .clr(in_1));
  Register IR_Op (.D(MBR_q), .en(iropld), .Q(IR_Op_q), .clk(clock_1_out), .clr(in_1));
  _8bit_ALU u_8bit_alu_1 (
    .A(multiplexer_2_out), .B(multiplexer_3_out), .V(n8bit_alu_1_v[0]), .Co(n8bit_alu_1_v[1]),
    .Z(n8bit_alu_1_v[2]), .S(n8bit_alu_1_v[3]), .F(n8bit_alu_1_f), .ALU(ALU));
  // Probe on add_lda_str_jmp_1_cnt
  // Probe on A
  ADD_LDA_STR_JMP add_lda_str_jmp_1 (
    .Ck(clock_1_out), .st(status_q), .RST(in_1), .IR_Op(IR_Op_q), .cnt(add_lda_str_jmp_1_cnt),
    .LDs({stld, iropld, marld, mbrld, iraddrld, pcld, acld}), .A(A), .B(B), .M(M), .ALU(ALU), .rw(rw));
  // Probe on n8bit_alu_1_f
  RAM ram_1 (.addr(MAR_q), .data(controlled_buffer_1_out), .sel(in_2), .clk(clock_1_out), .ld(rw));  // open: clr
endmodule

// CU2
module ADD_LDA_STR_JMP (
  input  Ck,
  input  [3:0] st,
  input  RST,
  input  [7:0] IR_Op,
  output [2:0] cnt,
  output [6:0] LDs,
  output [1:0] A,
  output [1:0] B,
  output M,
  output [5:0] ALU,
  output rw
);

  wire AC2BR, ADD, ADD_T4, ADD_T5, AND, BR2AC, BZ, IRAD2AR, IRAD2PC, JMP, LDA, LDA_T4, LDA_T5, NOP, NOT,
       not_1_out, OR, READ, SHL, SHR, STR, STR_T4, STR_T6, SUB, T0, T1, T4, T5, T6, T7, XOR;

  not not_1 (not_1_out, Ck);
  Counter #(.width(3), .max('h7)) u_cnt (.Q(cnt), .clk(not_1_out), .clr(RST));  // open: load, D, count, carry
  Decoder #(.select(3), .enable("false")) decoder_1 (
    .out0(T0), .out1(T1), .out2(LDs[1]), .out3(LDs[4]), .out4(T4), .out5(T5), .out6(T6), .out7(T7), .sel(cnt));
  and and_1 (LDA_T4, LDA, T4);
  and and_2 (LDA_T5, LDA, T5);
  and and_3 (BR2AC, LDA, T6);
  or or_1 (IRAD2AR, LDA_T4, ADD_T4, STR_T4);
  or or_2 (A[0], T0, T1, LDs[1], LDs[4], BR2AC);
  or or_3 (A[1], LDs[4], IRAD2AR, IRAD2PC, BR2AC);
  or or_4 (M, T1, READ, LDs[1]);
  not not_2 (rw, STR_T6);
  and and_4 (ADD_T4, ADD, T4);
  and and_5 (ADD_T5, ADD, T5);
  and and_6 (ALU[3], ADD, T6);
  or or_5 (READ, ADD_T5, LDA_T5);
  and and_7 (STR_T4, STR, T4);
  and and_8 (AC2BR, STR, T5);
  and and_9 (STR_T6, STR, T6);
  or or_6 (LDs[2], T0, IRAD2AR, T1);
  or or_7 (LDs[3], T1, READ, AC2BR, LDs[1]);
  or or_8 (LDs[5], T1, IRAD2PC, LDs[1]);
  or or_9 (ALU[2], T1, LDs[1]);
  Decoder #(.select(4), .enable("false")) decoder_2 (
    .out0(NOP), .out1(NOT), .out2(SHL), .out3(SHR), .out4(JMP), .out5(BZ), .out8(LDA), .out9(ADD),
    .out10(SUB), .out11(AND), .out12(OR), .out13(XOR), .out15(STR), .sel(IR_Op[7:4]));  // open: out6, out7, out14
  or or_10 (LDs[6], BR2AC, ALU[3]);
  and and_10 (IRAD2PC, JMP, T4);

  assign {ALU[5:4], ALU[1:0]} = 4'b0000;
  assign B = {2{ALU[3]}};
  assign LDs[0] = LDs[6];

  // Other names for the same wires on the sheet: ADD_T6 = ALU[3]; uADD = ALU[3]; JMP_T4 = IRAD2PC; LDA_T6 = BR2AC;
  //   T2 = LDs[1]; T3 = LDs[4]; V = st[0]; C = st[1]; Z = st[2]; S = st[3]; STR_T5 = AC2BR; WRITE = STR_T6
endmodule
