// Logisim project prob_3.circ as structural Verilog: 19 circuits, main circuit HA
module HA (
  input  A,
  input  B,
  output out_3,
  output out_4
);

  xor xor_1 (out_3, A, B);
  and and_1 (out_4, A, B);
endmodule

module FA (
  input  A,
  input  B,
  input  Cin,
  output S,
  output Cout
);

  wire ha_1_out_3, ha_1_out_4, ha_2_out_4;

  HA ha_1 (.A(A), .B(B), .out_3(ha_1_out_3), .out_4(ha_1_out_4));
  HA ha_2 (.A(ha_1_out_3), .B(Cin), .out_3(S), .out_4(ha_2_out_4));
  or or_1 (Cout, ha_2_out_4, ha_1_out_4);
endmodule

module _4x1mux (
  input  S1,
  input  S0,
  input  I0,
  input  I1,
  input  I2,
  input  I3,
  output O
);

  wire and_1_out, and_2_out, and_3_out, and_4_out, not_1_out, not_2_out;

  not not_1 (not_1_out, S1);
  not not_2 (not_2_out, S0);
  and and_1 (and_1_out, not_2_out, not_1_out, I0);
  and and_2 (and_2_out, S0, not_1_out, I1);
  and and_3 (and_3_out, not_2_out, S1, I2);
  and and_4 (and_4_out, S0, S1, I3);
  or or_1 (O, and_1_out, and_2_out, and_3_out, and_4_out);
endmodule

// 2x1M
module _2x1mux (
  input  S,
  input  I0,
  input  I1,
  output O
);

  wire and_1_out, and_2_out, not_1_out;

  not not_1 (not_1_out, S);
  and and_1 (and_1_out, not_1_out, I0);
  and and_2 (and_2_out, S, I1);
  or or_1 (O, and_1_out, and_2_out);
endmodule

module _4SH (
  input  SLin,
  input  [3:0] I,
  input  SRin,
  input  S1,
  input  S0,
  output [3:0] O
);

  _4x1mux u_4x1mux_1 (.S1(S1), .S0(S0), .I0(I[0]), .I1(I[1]), .I2(SLin), .I3(1'b0), .O(O[0]));
  _4x1mux u_4x1mux_2 (.S1(S1), .S0(S0), .I0(I[1]), .I1(I[2]), .I2(I[0]), .I3(1'b0), .O(O[1]));
  _4x1mux u_4x1mux_3 (.S1(S1), .S0(S0), .I0(I[2]), .I1(I[3]), .I2(I[1]), .I3(1'b0), .O(O[2]));
  _4x1mux u_4x1mux_4 (.S1(S1), .S0(S0), .I0(I[3]), .I1(SRin), .I2(I[2]), .I3(1'b0), .O(O[3]));
endmodule

module _8SH (
  input  SLin,
  input  [7:0] I,
  input  SRin,
  input  S1,
  input  S0,
  output [7:0] O
);

  _4SH u_4sh_1 (.SLin(SLin), .I(I[3:0]), .SRin(1'b0), .S1(S1), .S0(S0), .O(O[3:0]));
  _4SH u_4sh_2 (.SLin(1'b0), .I(I[7:4]), .SRin(SRin), .S1(S1), .S0(S0), .O(O[7:4]));
endmodule

module _1LU (
  input  A,
  input  B,
  input  S1,
  input  S0,
  output out_5
);

  wire and_1_out, not_1_out, or_1_out, xor_1_out;

  and and_1 (and_1_out, A, B);
  or or_1 (or_1_out, A, B);
  xor xor_1 (xor_1_out, A, B);
  not not_1 (not_1_out, A);
  _4x1mux u_4x1mux_1 (.S1(S1), .S0(S0), .I0(and_1_out), .I1(or_1_out), .I2(xor_1_out), .I3(not_1_out), .O(out_5));
endmodule

module _4LU (
  input  [3:0] A,
  input  [3:0] B,
  input  S1,
  input  S0,
  output [3:0] F
);

  _1LU u_1lu_1 (.A(A[0]), .B(B[0]), .S1(S1), .S0(S0), .out_5(F[0]));
  _1LU u_1lu_2 (.A(A[1]), .B(B[1]), .S1(S1), .S0(S1), .out_5(F[1]));
  _1LU u_1lu_3 (.A(A[2]), .B(B[2]), .S1(S1), .S0(S1), .out_5(F[2]));
  _1LU u_1lu_4 (.A(A[3]), .B(B[3]), .S1(S1), .S0(S1), .out_5(F[3]));
endmodule

module _8LU (
  input  [7:0] A,
  input  [7:0] B,
  input  S1,
  input  S0,
  output [7:0] out_5
);

  _4LU u_4lu_1 (.A(A[3:0]), .B(B[3:0]), .S1(S1), .S0(S0), .F(out_5[3:0]));
  _4LU u_4lu_2 (.A(A[7:4]), .B(B[7:4]), .S1(S1), .S0(S0), .F(out_5[7:4]));
endmodule

// 1AU
module _1bit_AU (
  input  Ci,
  input  A,
  input  B,
  input  S1,
  input  S0,
  output F,
  output Co
);

  wire n4x1mux_1_o, not_1_out;

  not not_1 (not_1_out, B);
  FA fa_1 (.A(A), .B(n4x1mux_1_o), .Cin(Ci), .S(F), .Cout(Co));
  _4x1mux u_4x1mux_1 (.S1(S1), .S0(S0), .I0(1'b0), .I1(B), .I2(not_1_out), .I3(1'b1), .O(n4x1mux_1_o));
endmodule

// 4AU
module _4bit_AU (
  input  Ci,
  input  [3:0] A,
  input  [3:0] B,
  input  S1,
  input  S0,
  output [3:0] F,
  output V,
  output Co
);

  wire n1bit_au_1_co, n1bit_au_2_co, n1bit_au_3_co;

  _1bit_AU u_1bit_au_1 (.A(A[0]), .B(B[0]), .S1(S1), .F(F[0]), .S0(S0), .Ci(Ci), .Co(n1bit_au_1_co));
  _1bit_AU u_1bit_au_2 (.A(A[1]), .B(B[1]), .S1(S1), .F(F[1]), .S0(S0), .Ci(n1bit_au_1_co), .Co(n1bit_au_2_co));
  _1bit_AU u_1bit_au_3 (.A(A[2]), .B(B[2]), .S1(S1), .F(F[2]), .S0(S0), .Ci(n1bit_au_2_co), .Co(n1bit_au_3_co));
  _1bit_AU u_1bit_au_4 (.A(A[3]), .B(B[3]), .S1(S1), .F(F[3]), .S0(S0), .Ci(n1bit_au_3_co), .Co(Co));
  xor xor_1 (V, n1bit_au_3_co, Co);
endmodule

// 8AU
module _8bit_AU (
  input  Ci,
  input  [7:0] A,
  input  [7:0] B,
  input  S1,
  input  S0,
  output [7:0] F,
  output V,
  output Co
);

  wire n1bit_au_1_co, n1bit_au_2_co, n1bit_au_3_co, n1bit_au_4_co, n1bit_au_5_co, n1bit_au_6_co,
       n1bit_au_7_co;

  _1bit_AU u_1bit_au_1 (.A(A[0]), .B(B[0]), .S1(S1), .F(F[0]), .S0(S0), .Ci(Ci), .Co(n1bit_au_1_co));
  _1bit_AU u_1bit_au_2 (.A(A[1]), .B(B[1]), .S1(S1), .F(F[1]), .S0(S0), .Ci(n1bit_au_1_co), .Co(n1bit_au_2_co));
  _1bit_AU u_1bit_au_3 (.A(A[2]), .B(B[2]), .S1(S1), .F(F[2]), .S0(S0), .Ci(n1bit_au_2_co), .Co(n1bit_au_3_co));
  _1bit_AU u_1bit_au_4 (.A(A[3]), .B(B[3]), .S1(S1), .F(F[3]), .S0(S0), .Ci(n1bit_au_3_co), .Co(n1bit_au_4_co));
  _1bit_AU u_1bit_au_5 (.A(A[4]), .B(B[4]), .S1(S1), .F(F[4]), .S0(S0), .Ci(n1bit_au_4_co), .Co(n1bit_au_5_co));
  _1bit_AU u_1bit_au_6 (.A(A[5]), .B(B[5]), .S1(S1), .F(F[5]), .S0(S0), .Ci(n1bit_au_5_co), .Co(n1bit_au_6_co));
  _1bit_AU u_1bit_au_7 (.A(A[6]), .B(B[6]), .S1(S1), .F(F[6]), .S0(S0), .Ci(n1bit_au_6_co), .Co(n1bit_au_7_co));
  _1bit_AU u_1bit_au_8 (.A(A[7]), .B(B[7]), .S1(S1), .F(F[7]), .S0(S0), .Ci(n1bit_au_7_co), .Co(Co));
  xor xor_1 (V, n1bit_au_7_co, Co);
endmodule

// 4 2x1
module _4bit_2x1_MUX (
  input  [3:0] A,
  input  [3:0] B,
  input  S,
  output [3:0] O
);

  _2x1mux u_2x1mux_1 (.S(A[0]), .I0(B[0]), .I1(S), .O(O[0]));
  _2x1mux u_2x1mux_2 (.S(A[1]), .I0(B[1]), .I1(S), .O(O[1]));
  _2x1mux u_2x1mux_3 (.S(A[2]), .I0(B[2]), .I1(S), .O(O[2]));
  _2x1mux u_2x1mux_4 (.S(A[3]), .I0(B[3]), .I1(S), .O(O[3]));
endmodule

// 8 2x1
module _8bit_2x1_MUX (
  input  [7:0] A,
  input  [7:0] B,
  input  S,
  output [7:0] O
);

  wire not_1_out;

  not not_1 (not_1_out, S);
  _2x1mux u_2x1mux_1 (.S(A[0]), .I0(B[0]), .I1(not_1_out), .O(O[0]));
  _2x1mux u_2x1mux_2 (.S(A[1]), .I0(B[1]), .I1(not_1_out), .O(O[1]));
  _2x1mux u_2x1mux_3 (.S(A[2]), .I0(B[2]), .I1(not_1_out), .O(O[2]));
  _2x1mux u_2x1mux_4 (.S(A[3]), .I0(B[3]), .I1(not_1_out), .O(O[3]));
  _2x1mux u_2x1mux_5 (.S(A[4]), .I0(B[4]), .I1(not_1_out), .O(O[4]));
  _2x1mux u_2x1mux_6 (.S(A[5]), .I0(B[5]), .I1(not_1_out), .O(O[5]));
  _2x1mux u_2x1mux_7 (.S(A[6]), .I0(B[6]), .I1(not_1_out), .O(O[6]));
  _2x1mux u_2x1mux_8 (.S(A[7]), .I0(B[7]), .I1(not_1_out), .O(O[7]));
endmodule

module _4bit_ALU (
  input  [3:0] A,
  input  [3:0] B,
  input  S2,
  input  S1,
  input  S0,
  input  H1,
  input  Ci,
  input  H0,
  output V,
  output Co,
  output Z,
  output S,
  output [3:0] F
);

  wire [3:0] n4bit_2x1_mux_1_o, n4bit_au_1_f, n4lu_1_f;

  _4bit_AU u_4bit_au_1 (.A(A), .B(B), .S1(S1), .S0(S0), .F(n4bit_au_1_f), .V(V), .Co(Co), .Ci(Ci));
  _4LU u_4lu_1 (.A(A), .B(B), .S1(S1), .S0(S0), .F(n4lu_1_f));
  _4bit_2x1_MUX u_4bit_2x1_mux_1 (.A(n4bit_au_1_f), .B(n4lu_1_f), .O(n4bit_2x1_mux_1_o), .S(S2));
  _4SH u_4sh_1 (.SLin(1'b0), .I(n4bit_2x1_mux_1_o), .SRin(1'b0), .S1(H1), .S0(H0), .O(F));
  nor nor_1 (Z, F[0], F[1], F[2], F[3]);

  assign S = F[3];
endmodule

module _8bit_ALU (
  input  [7:0] A,
  input  [7:0] B,
  input  [5:0] S210CiH10,
  output V,
  output Co,
  output Z,
  output S,
  output [7:0] F
);

  wire [7:0] n8bit_2x1_mux_1_o, n8bit_au_1_f, n8lu_1_out_5;

  _8bit_AU u_8bit_au_1 (
    .A(A), .B(B), .S1(S210CiH10[4]), .S0(S210CiH10[3]), .F(n8bit_au_1_f), .V(V), .Co(Co), .Ci(S210CiH10[2]));
  _8LU u_8lu_1 (.A(A), .B(B), .S1(S210CiH10[4]), .S0(S210CiH10[3]), .out_5(n8lu_1_out_5));
  _8SH u_8sh_1 (.SLin(1'b0), .SRin(1'b0), .S1(S210CiH10[1]), .S0(S210CiH10[0]), .O(F), .I(n8bit_2x1_mux_1_o));
  _8bit_2x1_MUX u_8bit_2x1_mux_1 (.A(n8bit_au_1_f), .B(n8lu_1_out_5), .O(n8bit_2x1_mux_1_o), .S(S210CiH10[5]));
  nor nor_1 (Z, F[0], F[1], F[2], F[3], F[4], F[5], F[6], F[7]);

  assign S = F[7];
endmodule

module MicroOperator (
  input  in_1,
  input  in_2
);

  wire acld, clock_1_out, iraddrld, iropld, M, marld, mbrld, not_1_out, pcld, rw, stld;
  wire [1:0] A, B;
  wire [2:0] control_unit_1_cnt;
  wire [3:0] n8bit_alu_1_v, register_1_q;
  wire [5:0] ALU;
  wire [7:0] AC_q, controlled_buffer_1_out, IR_Addr_q, IR_Op_q, MAR_q, MBR_q, multiplexer_1_out,
       multiplexer_2_out, multiplexer_3_out, n8bit_alu_1_f, PC_q;

  // Probe on M
  Multiplexer #(.width(8), .enable("false")) multiplexer_1 (
    .in0(n8bit_alu_1_f), .in1(controlled_buffer_1_out), .out(multiplexer_1_out), .sel(M));
  Clock clock_1 (.out(clock_1_out));
  Register AC (.D(n8bit_alu_1_f), .en(acld), .Q(AC_q), .clk(clock_1_out), .clr(in_1));
  Register PC (.D(n8bit_alu_1_f), .en(pcld), .Q(PC_q), .clk(clock_1_out), .clr(in_1));
  Register IR_Addr (.D(n8bit_alu_1_f), .en(iraddrld), .Q(IR_Addr_q), .clk(clock_1_out), .clr(in_1));
  Register MBR (.D(multiplexer_1_out), .en(mbrld), .Q(MBR_q), .clk(clock_1_out), .clr(in_1));
  Register MAR (.D(n8bit_alu_1_f), .en(marld), .Q(MAR_q), .clk(clock_1_out), .clr(in_1));
  assign controlled_buffer_1_out = not_1_out ? MBR_q : 8'bz;  // Controlled_Buffer controlled_buffer_1
  not not_1 (not_1_out, rw);
  Multiplexer #(.select(2), .width(8), .enable("false")) multiplexer_2 (
    .in0(AC_q), .in1(PC_q), .in2(IR_Addr_q), .in3(MBR_q), .out(multiplexer_2_out), .sel(A));
  // Probe on multiplexer_2_out
  _8bit_ALU u_8bit_alu_1 (
    .A(multiplexer_2_out), .B(multiplexer_3_out), .V(n8bit_alu_1_v[0]), .Co(n8bit_alu_1_v[1]),
    .Z(n8bit_alu_1_v[2]), .F(n8bit_alu_1_f), .S(n8bit_alu_1_v[3]), .S210CiH10(ALU));
  // Probe on multiplexer_3_out
  Multiplexer #(.select(2), .width(8), .enable("false")) multiplexer_3 (
    .in0(AC_q), .in1(PC_q), .in2(IR_Addr_q), .in3(MBR_q), .out(multiplexer_3_out), .sel(B));
  Register #(.width(4)) register_1 (.D(n8bit_alu_1_v), .en(stld), .Q(register_1_q), .clk(clock_1_out), .clr(in_1));
  Register IR_Op (.D(MBR_q), .en(iropld), .Q(IR_Op_q), .clk(clock_1_out), .clr(in_1));
  // Probe on n8bit_alu_1_f
  // Probe on control_unit_1_cnt
  Control_Unit control_unit_1 (
    .status(register_1_q), .IRop(IR_Op_q), .Clerk(clock_1_out), .Reset(in_1), .cnt(control_unit_1_cnt),
    .A(A), .Memory(M), .rw(rw), .ALU(ALU), .LDs({acld, pcld, iraddrld, mbrld, marld, iropld, stld}), .B(B));
  RAM ram_1 (.addr(MAR_q), .data(controlled_buffer_1_out), .sel(in_2), .clk(clock_1_out), .ld(rw));  // open: clr
endmodule

module FA2 (
  input  A,
  input  B,
  input  Cin,
  output S,
  output Cout
);

  wire and_1_out, and_2_out, xor_1_out;

  xor xor_1 (xor_1_out, A, B);
  and and_1 (and_1_out, A, B);
  xor xor_2 (S, xor_1_out, Cin);
  and and_2 (and_2_out, xor_1_out, Cin);
  or or_1 (Cout, and_2_out, and_1_out);
endmodule

// CU
module Control_Unit (
  input  Clerk,
  input  Reset,
  input  [3:0] status,
  input  [7:0] IRop,
  output [2:0] cnt,
  output [1:0] A,
  output [6:0] LDs,
  output [1:0] B,
  output Memory,
  output [5:0] ALU,
  output rw
);

  wire AC2BR, ADD, ADD_T4, ADD_T5, AND, BR2AC, BZ, IRAD2AR, IRAD2PC, JMP, LDA, LDA_T4, LDA_T5, NOP, NOT,
       not_1_out, OR, READ, SHL, SHR, STR, STR_T4, STR_T6, SUB, T0, T1, T4, T5, T6, T7, XOR;

  Counter #(.width(3), .max('h7)) counter_1 (.Q(cnt), .clk(not_1_out), .clr(Reset));  // open: load, D, count, carry
  not not_1 (not_1_out, Clerk);
  and and_1 (LDA_T4, LDA, T4);
  and and_2 (LDA_T5, LDA, T5);
  and and_3 (BR2AC, LDA, T6);
  or or_1 (IRAD2AR, ADD_T4, LDA_T4, STR_T4);
  Decoder #(.select(3), .enable("false")) decoder_1 (
    .out0(T0), .out1(T1), .out2(LDs[1]), .out3(LDs[4]), .out4(T4), .out5(T5), .out6(T6), .out7(T7), .sel(cnt));
  Decoder #(.select(4), .enable("false")) decoder_2 (
    .out0(NOP), .out1(NOT), .out2(SHL), .out3(SHR), .out4(JMP), .out5(BZ), .out8(LDA), .out9(ADD),
    .out10(SUB), .out11(AND), .out12(OR), .out13(XOR), .out15(STR), .sel(IRop[7:4]));  // open: out6, out7, out14
  and and_4 (ADD_T4, ADD, T4);
  and and_5 (ADD_T5, ADD, T5);
  and and_6 (ALU[3], ADD, T6);
  or or_2 (READ, ADD_T5, LDA_T5);
  or or_3 (Memory, T1, READ, LDs[1]);
  not not_2 (rw, STR_T6);
  and and_7 (STR_T4, STR, T4);
  and and_8 (AC2BR, STR, T5);
  and and_9 (STR_T6, STR, T6);
  or or_4 (A[0], T0, T1, LDs[1], LDs[4], BR2AC);
  or or_5 (A[1], LDs[4], IRAD2AR, IRAD2PC, BR2AC);
  and and_10 (IRAD2PC, JMP, T4);
  or or_6 (ALU[2], T0, T1);
  or or_7 (LDs[6], BR2AC, ALU[3]);
  or or_8 (LDs[2], T0, IRAD2AR, T1);
  or or_9 (LDs[3], T1, READ, AC2BR, LDs[1]);
  or or_10 (LDs[5], T1, IRAD2PC, LDs[1]);

  assign {ALU[5:4], ALU[1:0]} = 4'b0000;
  assign B = {2{ALU[3]}};
  assign LDs[0] = LDs[6];

  // Other names for the same wires on the sheet: ADD_T6 = ALU[3]; uADD = ALU[3]; JMP_T4 = IRAD2PC; LDA_T6 = BR2AC;
  //   T2 = LDs[1]; T3 = LDs[4]; V = status[0]; C = status[1]; Z = status[2]; S = status[3]; STR_T5 = AC2BR;
  //   WRITE = STR_T6

  // Notes on the sheet:
  //   Myung-ryung uh
  //   Tunnel Cycle
  //   Control Beat
endmodule
