// Logisim project hw1.circ as structural Verilog: 7 circuits, main circuit main
module main (
  input  a,
  input  b,
  input  c,
  input  d,
  output x,
  output y
);

  wire and_1_out, and_2_out, nand_1_out, nand_2_out;

  nand nand_1 (nand_1_out, a, b);
  nand nand_2 (nand_2_out, c, d);
  and and_1 (and_1_out, a, b);
  and and_2 (and_2_out, c, d);
  nand nand_3 (x, nand_1_out, nand_2_out);
  or or_1 (y, and_1_out, and_2_out);
endmodule

module NAND (
  input  in_1,
  input  in_2,
  input  in_3,
  input  in_4,
  output out_5,
  output out_6
);

  wire and_1_out, not_1_out, not_2_out;

  not not_1 (not_1_out, in_3);
  not not_2 (not_2_out, in_4);
  not not_3 (out_5, and_1_out);
  and and_1 (and_1_out, in_1, in_2);
  or or_1 (out_6, not_1_out, not_2_out);
endmodule

module DeMorgan (
  input  a,
  input  b,
  input  c,
  input  d,
  output x,
  output y
);

  wire and_1_out, and_2_out, nand_1_out, nand_2_out;

  nand nand_1 (nand_1_out, a, b);
  nand nand_2 (nand_2_out, c, d);
  and and_1 (and_1_out, a, b);
  and and_2 (and_2_out, c, d);
  nand nand_3 (x, nand_1_out, nand_2_out);
  or or_1 (y, and_1_out, and_2_out);
endmodule

module RS_latch (
  input  R,
  input  S,
  input  nS,
  input  nR,
  output Q,
  output nQ,
  output Q_2,
  output nQ_2
);

  nor nor_1 (Q, R, nQ);
  nor nor_2 (nQ, Q, S);
  nand nand_1 (Q_2, nS, nQ_2);
  nand nand_2 (nQ_2, Q_2, nR);
endmodule

// HA
module half_adder (
  input  A,
  input  B,
  output S,
  output C
);

  xor xor_1 (S, A, B);
  and and_1 (C, A, B);
endmodule

// FA
module full_adder (
  input  A,
  input  B,
  input  Cin,
  output S,
  output Cout
);

  wire half_adder_1_c, half_adder_1_s, half_adder_2_c;

  half_adder half_adder_1 (.A(A), .B(B), .S(half_adder_1_s), .C(half_adder_1_c));
  half_adder half_adder_2 (.A(half_adder_1_s), .B(Cin), .S(S), .C(half_adder_2_c));
  or or_1 (Cout, half_adder_2_c, half_adder_1_c);
endmodule

module _4bit_adder (
  input  Cin,
  input  in_2,
  input  in_3,
  input  in_4,
  input  in_5,
  output Cout
);

  wire full_adder_1_cout, full_adder_2_cout, full_adder_3_cout;

  full_adder full_adder_1 (.Cin(Cin), .Cout(full_adder_1_cout));  // open: A, B, S
  full_adder full_adder_2 (.Cin(full_adder_1_cout), .Cout(full_adder_2_cout));  // open: A, B, S
  full_adder full_adder_3 (.Cin(full_adder_2_cout), .Cout(full_adder_3_cout));  // open: A, B, S
  full_adder full_adder_4 (.Cin(full_adder_3_cout), .Cout(Cout));  // open: A, B, S
endmodule
