// Logisim project hw2-flipflop.circ as structural Verilog
module SR_Latch (
  input  R,
  input  S,
  input  nS,
  input  nR,
  output Q,
  output nQ,
  output Q_2,
  output nQ_2
);

  nor nor_1 (Q, R, nQ);
  nor nor_2 (nQ, Q, S);
  nand nand_1 (Q_2, nS, nQ_2);
  nand nand_2 (nQ_2, Q_2, nR);
endmodule

module Gated_SR_Latch (
  input  R,
  input  E,
  input  S,
  output Q,
  output nQ
);

  wire and_1_out, and_2_out;

  and and_1 (and_1_out, R, E);
  and and_2 (and_2_out, E, S);
  nor nor_1 (Q, and_1_out, nQ);
  nor nor_2 (nQ, Q, and_2_out);
endmodule

// D latch
module Gated_D_Latch (
  input  clear,
  input  D,
  input  E,
  output Q,
  output nQ
);

  wire and_1_out, and_2_out, not_1_out;

  not not_1 (not_1_out, D);
  and and_1 (and_1_out, not_1_out, E);
  and and_2 (and_2_out, E, D);
  nor nor_1 (Q, clear, and_1_out, nQ);
  nor nor_2 (nQ, Q, and_2_out);
endmodule

// D latch
module Gated_D_Latch_orig (
  input  D,
  input  E,
  output Q,
  output nQ
);

  wire and_1_out, and_2_out, not_1_out;

  not not_1 (not_1_out, D);
  and and_1 (and_1_out, not_1_out, E);
  and and_2 (and_2_out, E, D);
  nor nor_1 (Q, and_1_out, nQ);
  nor nor_2 (nQ, Q, and_2_out);
endmodule

// D FF
module MS_D_Flip_flop (
  input  in_1,
  input  D,
  input  Ck,
  output Q,
  output nQ
);

  wire gated_d_latch_1_q, not_1_out;

  Gated_D_Latch gated_d_latch_1 (.D(D), .E(not_1_out), .Q(gated_d_latch_1_q), .clear(1'b0));  // open: nQ
  not not_1 (not_1_out, Ck);
  Gated_D_Latch gated_d_latch_2 (.D(gated_d_latch_1_q), .E(Ck), .Q(Q), .nQ(nQ), .clear(in_1));
endmodule

// D FF
module MS_D_Flip_flop_orig (
  input  D,
  input  Ck,
  output Q,
  output nQ
);

  wire gated_d_latch_orig_1_q, not_1_out;

  Gated_D_Latch_orig gated_d_latch_orig_1 (.D(D), .E(not_1_out), .Q(gated_d_latch_orig_1_q));  // open: nQ
  not not_1 (not_1_out, Ck);
  Gated_D_Latch_orig gated_d_latch_orig_2 (.D(gated_d_latch_orig_1_q), .E(Ck), .Q(Q), .nQ(nQ));
endmodule

module _4bit_register (
  input  [3:0] D,
  input  clear,
  input  Ck,
  input  E,
  output [3:0] Q
);

  wire and_1_out;

  and and_1 (and_1_out, Ck, E);
  MS_D_Flip_flop ms_d_flip_flop_1 (.D(D[0]), .Ck(and_1_out), .Q(Q[0]), .in_1(clear));  // open: nQ
  MS_D_Flip_flop ms_d_flip_flop_2 (.D(D[1]), .Ck(and_1_out), .Q(Q[1]), .in_1(clear));  // open: nQ
  MS_D_Flip_flop ms_d_flip_flop_3 (.D(D[2]), .Ck(and_1_out), .Q(Q[2]), .in_1(clear));  // open: nQ
  MS_D_Flip_flop ms_d_flip_flop_4 (.D(D[3]), .Ck(and_1_out), .Q(Q[3]), .in_1(clear));  // open: nQ
endmodule

module _4bit_register_orig (
  input  [3:0] D,
  input  Ck,
  output [3:0] Q
);

  MS_D_Flip_flop_orig ms_d_flip_flop_orig_1 (.D(D[0]), .Ck(Ck), .Q(Q[0]));  // open: nQ
  MS_D_Flip_flop_orig ms_d_flip_flop_orig_2 (.D(D[1]), .Ck(Ck), .Q(Q[1]));  // open: nQ
  MS_D_Flip_flop_orig ms_d_flip_flop_orig_3 (.D(D[2]), .Ck(Ck), .Q(Q[2]));  // open: nQ
  MS_D_Flip_flop_orig ms_d_flip_flop_orig_4 (.D(D[3]), .Ck(Ck), .Q(Q[3]));  // open: nQ
endmodule

module _8bit_register (
  input  [7:0] D,
  input  Ck,
  input  E,
  input  clear,
  output [7:0] Q
);

  wire and_1_out;

  and and_1 (and_1_out, Ck, E);
  MS_D_Flip_flop ms_d_flip_flop_1 (.D(D[0]), .Ck(and_1_out), .Q(Q[0]), .in_1(clear));  // open: nQ
  MS_D_Flip_flop ms_d_flip_flop_2 (.D(D[1]), .Ck(and_1_out), .Q(Q[1]), .in_1(clear));  // open: nQ
  MS_D_Flip_flop ms_d_flip_flop_3 (.D(D[2]), .Ck(and_1_out), .Q(Q[2]), .in_1(clear));  // open: nQ
  MS_D_Flip_flop ms_d_flip_flop_4 (.D(D[3]), .Ck(and_1_out), .Q(Q[3]), .in_1(clear));  // open: nQ
  MS_D_Flip_flop ms_d_flip_flop_5 (.D(D[4]), .Ck(and_1_out), .Q(Q[4]), .in_1(clear));  // open: nQ
  MS_D_Flip_flop ms_d_flip_flop_6 (.D(D[5]), .Ck(and_1_out), .Q(Q[5]), .in_1(clear));  // open: nQ
  MS_D_Flip_flop ms_d_flip_flop_7 (.D(D[6]), .Ck(and_1_out), .Q(Q[6]), .in_1(clear));  // open: nQ
  MS_D_Flip_flop ms_d_flip_flop_8 (.D(D[7]), .Ck(and_1_out), .Q(Q[7]), .in_1(clear));  // open: nQ
endmodule

module BC (
  input  Select,
  input  Input,
  input  RW,
  output Output
);

  wire and_1_out, and_2_out, nor_1_out, nor_2_out, not_1_out, not_2_out;

  and and_1 (and_1_out, Select, not_1_out, not_2_out);
  not not_1 (not_1_out, Input);
  and and_2 (and_2_out, Select, Input, not_2_out);
  not not_2 (not_2_out, RW);
  nor nor_1 (nor_1_out, and_1_out, nor_2_out);
  nor nor_2 (nor_2_out, nor_1_out, and_2_out);
  and and_3 (Output, Select, nor_1_out, RW);
endmodule

module _4x4_RAM (
  input  [3:0] DataIn,
  input  E,
  input  [1:0] Addr,
  input  RW,
  output [3:0] DataOut
);

  wire bc_1_output, bc_2_output, bc_3_output, bc_4_output, bc_5_output, bc_6_output, bc_7_output,
       bc_8_output, bc_9_output, bc_10_output, bc_11_output, bc_12_output, bc_13_output, bc_14_output,
       bc_15_output, bc_16_output, decoder_1_out0, decoder_1_out1, decoder_1_out2, decoder_1_out3;

  Decoder #(.select(2), .disabled(0)) decoder_1 (
    .out0(decoder_1_out0), .out1(decoder_1_out1), .out2(decoder_1_out2), .out3(decoder_1_out3), .sel(Addr),
    .en(E));
  BC bc_1 (.Select(decoder_1_out0), .Input(DataIn[3]), .RW(RW), .Output(bc_1_output));
  BC bc_2 (.Select(decoder_1_out1), .Input(DataIn[3]), .RW(RW), .Output(bc_2_output));
  BC bc_3 (.Select(decoder_1_out2), .Input(DataIn[3]), .RW(RW), .Output(bc_3_output));
  BC bc_4 (.Select(decoder_1_out3), .Input(DataIn[3]), .RW(RW), .Output(bc_4_output));
  or or_1 (DataOut[3], bc_4_output, bc_3_output, bc_2_output, bc_1_output);
  BC bc_5 (.Select(decoder_1_out0), .Input(DataIn[2]), .RW(RW), .Output(bc_5_output));
  BC bc_6 (.Select(decoder_1_out1), .Input(DataIn[2]), .RW(RW), .Output(bc_6_output));
  BC bc_7 (.Select(decoder_1_out2), .Input(DataIn[2]), .RW(RW), .Output(bc_7_output));
  BC bc_8 (.Select(decoder_1_out3), .Input(DataIn[2]), .RW(RW), .Output(bc_8_output));
  BC bc_9 (.Select(decoder_1_out0), .Input(DataIn[1]), .RW(RW), .Output(bc_9_output));
  BC bc_10 (.Select(decoder_1_out1), .Input(DataIn[1]), .RW(RW), .Output(bc_10_output));
  BC bc_11 (.Select(decoder_1_out2), .Input(DataIn[1]), .RW(RW), .Output(bc_11_output));
  BC bc_12 (.Select(decoder_1_out3), .Input(DataIn[1]), .RW(RW), .Output(bc_12_output));
  or or_2 (DataOut[2], bc_8_output, bc_7_output, bc_6_output, bc_5_output);
  or or_3 (DataOut[1], bc_12_output, bc_11_output, bc_10_output, bc_9_output);
  BC bc_13 (.Select(decoder_1_out0), .Input(DataIn[0]), .RW(RW), .Output(bc_13_output));
  BC bc_14 (.Select(decoder_1_out1), .Input(DataIn[0]), .RW(RW), .Output(bc_14_output));
  BC bc_15 (.Select(decoder_1_out2), .Input(DataIn[0]), .RW(RW), .Output(bc_15_output));
  BC bc_16 (.Select(decoder_1_out3), .Input(DataIn[0]), .RW(RW), .Output(bc_16_output));
  or or_4 (DataOut[0], bc_16_output, bc_15_output, bc_14_output, bc_13_output);
endmodule
