// Logisim project hw3-decoder mux.circ as structural Verilog
module _1x2_decoder (
  input  C0,
  output D0,
  output D1
);

  not not_1 (D0, C0);

  assign D1 = C0;
endmodule

// 2x4
module _2x4_decoder (
  input  C1,
  input  C0,
  output D0,
  output D1,
  output D2,
  output D3
);

  wire not_1_out, not_2_out;

  not not_1 (not_1_out, C1);
  not not_2 (not_2_out, C0);
  and and_1 (D0, not_2_out, not_1_out);
  and and_2 (D1, C0, not_1_out);
  and and_3 (D2, not_2_out, C1);
  and and_4 (D3, C0, C1);
endmodule

module _3x8_decoder (
  input  C2,
  input  C1,
  input  C0,
  input  E,
  output out_5,
  output out_6,
  output out_7,
  output out_8,
  output out_9,
  output out_10,
  output out_11,
  output out_12
);

  wire not_1_out, not_2_out, not_3_out;

  not not_1 (not_1_out, C2);
  not not_2 (not_2_out, C1);
  not not_3 (not_3_out, C0);
  and and_1 (out_5, not_1_out, not_2_out, not_3_out, E);
  and and_2 (out_6, not_1_out, not_2_out, C0, E);
  and and_3 (out_7, not_1_out, C1, not_3_out, E);
  and and_4 (out_8, not_1_out, C1, C0, E);
  and and_5 (out_9, C2, not_2_out, not_3_out, E);
  and and_6 (out_10, C2, not_2_out, C0, E);
  and and_7 (out_11, C2, C1, not_3_out, E);
  and and_8 (out_12, C2, C1, C0, E);
endmodule
