// Logisim project hw4-AU_status.circ as structural Verilog
// FA
module full_adder (
  input  A,
  input  B,
  input  Cin,
  output S,
  output Cout
);

  wire and_1_out, and_2_out, and_3_out, and_4_out, and_5_out, and_6_out, and_7_out, not_1_out, not_2_out,
       not_3_out, not_4_out, not_5_out, not_6_out;

  not not_1 (not_1_out, A);
  not not_2 (not_2_out, B);
  not not_3 (not_3_out, A);
  not not_4 (not_4_out, Cin);
  not not_5 (not_5_out, B);
  not not_6 (not_6_out, Cin);
  and and_1 (and_1_out, B, Cin);
  and and_2 (and_2_out, A, Cin);
  and and_3 (and_3_out, A, B);
  and and_4 (and_4_out, not_1_out, not_2_out, Cin);
  and and_5 (and_5_out, not_3_out, B, not_4_out);
  and and_6 (and_6_out, A, not_5_out, not_6_out);
  and and_7 (and_7_out, A, B, Cin);
  or or_1 (Cout, and_1_out, and_2_out, and_3_out);
  or or_2 (S, and_4_out, and_5_out, and_6_out, and_7_out);
endmodule

module _1_AU (
  input  Ci,
  input  A,
  input  B,
  input  S1,
  input  S0,
  output F,
  output Co
);

  wire and_1_out, and_2_out, not_1_out, or_1_out;

  not not_1 (not_1_out, B);
  and and_1 (and_1_out, not_1_out, S1);
  and and_2 (and_2_out, B, S0);
  or or_1 (or_1_out, and_1_out, and_2_out);
  full_adder full_adder_1 (.A(A), .B(or_1_out), .Cin(Ci), .S(F), .Cout(Co));
endmodule

module _4bit_AU (
  input  Ci,
  input  [3:0] A,
  input  [3:0] B,
  input  S1,
  input  S0,
  output [3:0] out_6,
  output Co
);

  wire n1_au_1_co, n1_au_2_co, n1_au_3_co;

  _1_AU u_1_au_1 (.Ci(Ci), .A(A[0]), .B(B[0]), .S1(S1), .S0(S0), .F(out_6[0]), .Co(n1_au_1_co));
  _1_AU u_1_au_2 (.Ci(n1_au_1_co), .A(A[1]), .B(B[1]), .S1(S1), .S0(S0), .F(out_6[1]), .Co(n1_au_2_co));
  _1_AU u_1_au_3 (.Ci(n1_au_2_co), .A(A[2]), .B(B[2]), .S1(S1), .S0(S0), .F(out_6[2]), .Co(n1_au_3_co));
  _1_AU u_1_au_4 (.Ci(n1_au_3_co), .A(A[3]), .B(B[3]), .S1(S1), .S0(S0), .F(out_6[3]), .Co(Co));
endmodule
