// Logisim project hw5-counter_decoder.circ as structural Verilog: 13 circuits, main circuit main
module main (
  input  in_1,
  input  [2:0] in_2,
  input  in_3,
  input  [2:0] in_4,
  output [7:0] out_5,
  output [7:0] out_6
);

  Demultiplexer #(.select(3), .enable("false")) demultiplexer_1 (
    .out0(out_5[0]), .out1(out_5[1]), .out2(out_5[2]), .out3(out_5[3]), .out4(out_5[4]), .out5(out_5[5]),
    .out6(out_5[6]), .out7(out_5[7]), .in(in_1), .sel(in_2));
  Decoder #(.select(3)) decoder_1 (
    .out0(out_6[0]), .out1(out_6[1]), .out2(out_6[2]), .out3(out_6[3]), .out4(out_6[4]), .out5(out_6[5]),
    .out6(out_6[6]), .out7(out_6[7]), .sel(in_4), .en(in_3));
endmodule

module SR_Latch (
  input  R,
  input  S,
  input  nS,
  input  nR,
  output Q,
  output nQ,
  output Q_2,
  output nQ_2
);

  nor nor_1 (Q, R, nQ);
  nor nor_2 (nQ, Q, S);
  nand nand_1 (Q_2, nS, nQ_2);
  nand nand_2 (nQ_2, Q_2, nR);
endmodule

module Gated_SR_Latch (
  input  R,
  input  E,
  input  S,
  output Q,
  output nQ
);

  wire and_1_out, and_2_out;

  and and_1 (and_1_out, R, E);
  and and_2 (and_2_out, E, S);
  nor nor_1 (Q, and_1_out, nQ);
  nor nor_2 (nQ, Q, and_2_out);
endmodule

// D latch
module Gated_D_Latch (
  input  clear,
  input  D,
  input  E,
  output Q,
  output nQ
);

  wire and_1_out, and_2_out, not_1_out;

  not not_1 (not_1_out, D);
  and and_1 (and_1_out, not_1_out, E);
  and and_2 (and_2_out, E, D);
  nor nor_1 (Q, clear, and_1_out, nQ);
  nor nor_2 (nQ, Q, and_2_out);
endmodule

// D FF
module MS_D_Flip_flop (
  input  in_1,
  input  D,
  input  Ck,
  output Q,
  output nQ
);

  wire gated_d_latch_1_q, not_1_out;

  Gated_D_Latch gated_d_latch_1 (.D(D), .E(not_1_out), .Q(gated_d_latch_1_q), .clear(1'b0));  // open: nQ
  not not_1 (not_1_out, Ck);
  Gated_D_Latch gated_d_latch_2 (.D(gated_d_latch_1_q), .E(Ck), .Q(Q), .nQ(nQ), .clear(in_1));
endmodule

module _4bit_register (
  input  [3:0] D,
  input  clear,
  input  Ck,
  input  E,
  output [3:0] Q
);

  wire and_1_out;

  and and_1 (and_1_out, Ck, E);
  MS_D_Flip_flop ms_d_flip_flop_1 (.D(D[0]), .Ck(and_1_out), .Q(Q[0]), .in_1(clear));  // open: nQ
  MS_D_Flip_flop ms_d_flip_flop_2 (.D(D[1]), .Ck(and_1_out), .Q(Q[1]), .in_1(clear));  // open: nQ
  MS_D_Flip_flop ms_d_flip_flop_3 (.D(D[2]), .Ck(and_1_out), .Q(Q[2]), .in_1(clear));  // open: nQ
  MS_D_Flip_flop ms_d_flip_flop_4 (.D(D[3]), .Ck(and_1_out), .Q(Q[3]), .in_1(clear));  // open: nQ
endmodule

module _8bit_register (
  input  [7:0] D,
  input  Ck,
  input  E,
  input  clear,
  output [7:0] Q
);

  wire and_1_out;

  and and_1 (and_1_out, Ck, E);
  MS_D_Flip_flop ms_d_flip_flop_1 (.D(D[0]), .Ck(and_1_out), .Q(Q[0]), .in_1(clear));  // open: nQ
  MS_D_Flip_flop ms_d_flip_flop_2 (.D(D[1]), .Ck(and_1_out), .Q(Q[1]), .in_1(clear));  // open: nQ
  MS_D_Flip_flop ms_d_flip_flop_3 (.D(D[2]), .Ck(and_1_out), .Q(Q[2]), .in_1(clear));  // open: nQ
  MS_D_Flip_flop ms_d_flip_flop_4 (.D(D[3]), .Ck(and_1_out), .Q(Q[3]), .in_1(clear));  // open: nQ
  MS_D_Flip_flop ms_d_flip_flop_5 (.D(D[4]), .Ck(and_1_out), .Q(Q[4]), .in_1(clear));  // open: nQ
  MS_D_Flip_flop ms_d_flip_flop_6 (.D(D[5]), .Ck(and_1_out), .Q(Q[5]), .in_1(clear));  // open: nQ
  MS_D_Flip_flop ms_d_flip_flop_7 (.D(D[6]), .Ck(and_1_out), .Q(Q[6]), .in_1(clear));  // open: nQ
  MS_D_Flip_flop ms_d_flip_flop_8 (.D(D[7]), .Ck(and_1_out), .Q(Q[7]), .in_1(clear));  // open: nQ
endmodule

module JK_filp_flop (
  input  in_1,
  input  in_2,
  input  in_3,
  output Q,
  output nQ
);

  wire nand_1_out, nand_2_out, nand_3_out, nand_4_out, nand_5_out, nand_6_out, not_1_out;

  not not_1 (not_1_out, in_2);
  nand nand_1 (nand_1_out, nQ, in_1, not_1_out);
  nand nand_2 (nand_2_out, not_1_out, in_3, Q);
  nand nand_3 (nand_3_out, nand_1_out, nand_4_out);
  nand nand_4 (nand_4_out, nand_3_out, nand_2_out);
  nand nand_5 (nand_5_out, nand_3_out, in_2);
  nand nand_6 (nand_6_out, in_2, nand_4_out);
  nand nand_7 (Q, nand_5_out, nQ);
  nand nand_8 (nQ, Q, nand_6_out);
endmodule

// JK
module JK_flip_flop2 (
  input  J,
  input  K,
  input  Ck,
  output Q,
  output Q_prime
);

  wire and_1_out, and_2_out, and_3_out, and_4_out, nand_1_out, nand_2_out, nor_1_out, nor_2_out, not_1_out;

  nand nand_1 (nand_1_out, Q, K);
  not not_1 (not_1_out, Ck);
  nand nand_2 (nand_2_out, J, Q_prime);
  and and_1 (and_1_out, nand_1_out, J, not_1_out);
  and and_2 (and_2_out, not_1_out, K, nand_2_out);
  nor nor_1 (nor_1_out, and_1_out, nor_2_out);
  nor nor_2 (nor_2_out, nor_1_out, and_2_out);
  and and_3 (and_3_out, nor_1_out, Ck);
  and and_4 (and_4_out, Ck, nor_2_out);
  nor nor_3 (Q, and_3_out, Q_prime);
  nor nor_4 (Q_prime, Q, and_4_out);
endmodule

module _4bit_counter (
  output [3:0] F
);

  wire and_1_out, and_2_out, Ck_out;

  Clock Ck (.out(Ck_out));
  and and_1 (and_1_out, F[2], and_2_out);
  T_Flip_Flop t_ff_1 (.clk(Ck_out), .T(and_1_out), .Q(F[3]), .en(1'b1));  // open: Qn, preset, reset
  and and_2 (and_2_out, F[0], F[1]);
  T_Flip_Flop t_ff_2 (.clk(Ck_out), .T(and_2_out), .Q(F[2]), .en(1'b1));  // open: Qn, preset, reset
  T_Flip_Flop t_ff_3 (.clk(Ck_out), .T(F[0]), .Q(F[1]), .en(1'b1));  // open: Qn, preset, reset
  T_Flip_Flop t_ff_4 (.clk(Ck_out), .T(1'b1), .Q(F[0]), .en(1'b1));  // open: Qn, preset, reset
endmodule

// 3x8
module _3x8_decoder (
  input  C2,
  input  C1,
  input  C0,
  input  E,
  output D0,
  output D1,
  output D2,
  output D3,
  output D4,
  output D5,
  output D6,
  output D7
);

  wire not_1_out, not_2_out, not_3_out;

  not not_1 (not_1_out, C1);
  not not_2 (not_2_out, C2);
  not not_3 (not_3_out, C0);
  and and_1 (D0, not_2_out, not_1_out, not_3_out, E);
  and and_2 (D1, not_2_out, not_1_out, C0, E);
  and and_3 (D2, not_2_out, C1, not_3_out, E);
  and and_4 (D3, not_2_out, C1, C0, E);
  and and_5 (D4, C2, not_1_out, not_3_out, E);
  and and_6 (D5, C2, not_1_out, C0, E);
  and and_7 (D6, C2, C1, not_3_out, E);
  and and_8 (D7, C2, C1, C0, E);
endmodule

module _4x16_decoder (
  input  C3,
  input  C2,
  input  C1,
  input  C0,
  output [15:0] D
);

  wire not_1_out;

  _3x8_decoder u_3x8_decoder_1 (
    .C2(C2), .C1(C1), .C0(C0), .E(not_1_out), .D0(D[0]), .D1(D[1]), .D2(D[2]), .D3(D[3]), .D4(D[4]),
    .D5(D[5]), .D6(D[6]), .D7(D[7]));
  not not_1 (not_1_out, C3);
  _3x8_decoder u_3x8_decoder_2 (
    .C2(C2), .C1(C1), .C0(C0), .E(C3), .D0(D[8]), .D1(D[9]), .D2(D[10]), .D3(D[11]), .D4(D[12]), .D5(D[13]),
    .D6(D[14]), .D7(D[15]));
endmodule

module decoder___dmx (
  input  in_1,
  input  [2:0] in_2,
  input  in_3,
  input  [2:0] in_4,
  output [7:0] out_5,
  output [7:0] out_6
);

  Demultiplexer #(.select(3), .enable("false")) demultiplexer_1 (
    .out0(out_5[0]), .out1(out_5[1]), .out2(out_5[2]), .out3(out_5[3]), .out4(out_5[4]), .out5(out_5[5]),
    .out6(out_5[6]), .out7(out_5[7]), .in(in_1), .sel(in_2));
  Decoder #(.select(3), .disabled(0)) decoder_1 (
    .out0(out_6[0]), .out1(out_6[1]), .out2(out_6[2]), .out3(out_6[3]), .out4(out_6[4]), .out5(out_6[5]),
    .out6(out_6[6]), .out7(out_6[7]), .sel(in_4), .en(in_3));
endmodule
