// Logisim project picoMIPS.circ as structural Verilog: 5 circuits, main circuit main
module main (
);

  wire [2:0] multiplexer_1_out;
  wire [15:0] adder_1_out, alu16_1_f, multiplexer_2_out, multiplexer_3_out, PC_q, ram_1_data, ram_2_data,
       regfile_16bit_x_8_1_rd1, regfile_16bit_x_8_1_rd2, undriven;

  Register #(.width(16)) PC (.D(adder_1_out), .Q(PC_q));  // open: en, clk, clr
  Adder #(.width(16)) adder_1 (.a(16'h4), .b(PC_q), .out(adder_1_out));  // open: cin, cout
  RAM #(.addrWidth(16), .dataWidth(16)) ram_1 (.addr(PC_q), .data(ram_1_data));  // open: sel, clk, ld, clr
  Multiplexer #(.width(3), .enable("false")) multiplexer_1 (
    .in0(ram_1_data[8:6]), .in1(ram_1_data[5:3]), .out(multiplexer_1_out));  // open: sel
  RegFile_16bit_x_8 regfile_16bit_x_8_1 (
    .WD(multiplexer_3_out), .WR(multiplexer_1_out), .RD1(regfile_16bit_x_8_1_rd1), .RR1(ram_1_data[11:9]),
    .RD2(regfile_16bit_x_8_1_rd2), .RR2(ram_1_data[8:6]));  // open: Write, Ck
  ALU16 alu16_1 (.A(regfile_16bit_x_8_1_rd1), .B(multiplexer_2_out), .F(alu16_1_f));  // open: ALUop
  Multiplexer #(.width(16), .enable("false")) multiplexer_2 (
    .in0(regfile_16bit_x_8_1_rd2), .in1(undriven), .out(multiplexer_2_out));  // open: sel
  RAM #(.addrWidth(16), .dataWidth(16), .bus("separate")) ram_2 (
    .addr(alu16_1_f), .din(regfile_16bit_x_8_1_rd2), .data(ram_2_data));  // open: str, sel, clk, ld, clr
  Multiplexer #(.width(16), .enable("false")) multiplexer_3 (
    .in0(ram_2_data), .in1(alu16_1_f), .out(multiplexer_3_out));  // open: sel
endmodule

// RegFile16x8
module RegFile_16bit_x_8 (
  input  [15:0] WD,
  input  [2:0] RR1,
  input  Write,
  input  [2:0] WR,
  input  [2:0] RR2,
  input  Ck,
  output [15:0] RD1,
  output [15:0] RD2
);

  wire decoder_1_out0, decoder_1_out1, decoder_1_out2, decoder_1_out3, decoder_1_out4, decoder_1_out5,
       decoder_1_out6, decoder_1_out7;
  wire [15:0] r0_q, r1_q, r2_q, r3_q, r4_q, r5_q, r6_q, r7_q;

  Decoder #(.select(3), .disabled(0)) decoder_1 (
    .out0(decoder_1_out0), .out1(decoder_1_out1), .out2(decoder_1_out2), .out3(decoder_1_out3),
    .out4(decoder_1_out4), .out5(decoder_1_out5), .out6(decoder_1_out6), .out7(decoder_1_out7), .sel(WR),
    .en(Write));
  Register #(.width(16)) r0 (.D(WD), .en(decoder_1_out0), .Q(r0_q), .clk(Ck));  // open: clr
  Register #(.width(16)) r1 (.D(WD), .en(decoder_1_out1), .Q(r1_q), .clk(Ck));  // open: clr
  Register #(.width(16)) r2 (.D(WD), .en(decoder_1_out2), .Q(r2_q), .clk(Ck));  // open: clr
  Register #(.width(16)) r3 (.D(WD), .en(decoder_1_out3), .Q(r3_q), .clk(Ck));  // open: clr
  Register #(.width(16)) r4 (.D(WD), .en(decoder_1_out4), .Q(r4_q), .clk(Ck));  // open: clr
  Register #(.width(16)) r5 (.D(WD), .en(decoder_1_out5), .Q(r5_q), .clk(Ck));  // open: clr
  Register #(.width(16)) r6 (.D(WD), .en(decoder_1_out6), .Q(r6_q), .clk(Ck));  // open: clr
  Register #(.width(16)) r7 (.D(WD), .en(decoder_1_out7), .Q(r7_q), .clk(Ck));  // open: clr
  Multiplexer #(.select(3), .width(16), .enable("false")) multiplexer_1 (
    .in0(r0_q), .in1(r1_q), .in2(r2_q), .in3(r3_q), .in4(r4_q), .in5(r5_q), .in6(r6_q), .in7(r7_q),
    .out(RD1), .sel(RR1));
  Multiplexer #(.select(3), .width(16), .enable("false")) multiplexer_2 (
    .in0(r0_q), .in1(r1_q), .in2(r2_q), .in3(r3_q), .in4(r4_q), .in5(r5_q), .in6(r6_q), .in7(r7_q),
    .out(RD2), .sel(RR2));
endmodule

module ALU16 (
  input  [15:0] A,
  input  [2:0] ALUop,
  input  [15:0] B,
  output [15:0] F
);

  wire [15:0] adder_1_out, and_1_out, divider_1_out, multiplier_1_out, or_1_out, subtractor_1_out;

  assign and_1_out = A & B;  // AND_Gate and_1, 16 bits wide
  assign or_1_out = A | B;  // OR_Gate or_1, 16 bits wide
  Adder #(.width(16)) adder_1 (.a(A), .b(B), .out(adder_1_out));  // open: cin, cout
  Subtractor #(.width(16)) subtractor_1 (.a(A), .b(B), .out(subtractor_1_out));  // open: bin, bout
  Multiplier #(.width(16)) multiplier_1 (.a(A), .b(B), .out(multiplier_1_out));  // open: cin, cout
  Divider #(.width(16)) divider_1 (.a(A), .b(B), .out(divider_1_out));  // open: upper, rem
  Multiplexer #(.select(3), .width(16), .enable("false")) multiplexer_1 (
    .in0(and_1_out), .in1(or_1_out), .in2(adder_1_out), .in3(subtractor_1_out), .in4(multiplier_1_out),
    .in5(divider_1_out), .out(F), .sel(ALUop));  // open: in6, in7
endmodule

module Single_Cycle_Datapath (
);

  wire [2:0] fn, multiplexer_1_out;
  wire [3:0] Op;
  wire [11:3] ram_1_data;
  wire [15:0] adder_1_out, adder_2_out, alu16_1_f, multiplexer_2_out, multiplexer_3_out, multiplexer_4_out,
       PC_q, ram_2_data, regfile_16bit_x_8_1_rd1, regfile_16bit_x_8_1_rd2, shifter_1_out,
       signext_6_to_16bit_1_out;

  Register #(.width(16)) PC (.D(multiplexer_3_out), .Q(PC_q));  // open: en, clk, clr
  Adder #(.width(16)) adder_1 (.a(16'h2), .b(PC_q), .out(adder_1_out));  // open: cin, cout
  RAM #(.addrWidth(16), .dataWidth(16)) ram_1 (.addr(PC_q), .data({Op, ram_1_data, fn}));  // open: sel, clk, ld, clr
  Multiplexer #(.width(3), .enable("false")) multiplexer_1 (
    .in0(ram_1_data[8:6]), .in1(ram_1_data[5:3]), .out(multiplexer_1_out));  // open: sel
  SignExt_6_to_16bit signext_6_to_16bit_1 (.In({ram_1_data[5:3], fn}), .Out(signext_6_to_16bit_1_out));
  RegFile_16bit_x_8 regfile_16bit_x_8_1 (
    .WD(multiplexer_4_out), .WR(multiplexer_1_out), .RD1(regfile_16bit_x_8_1_rd1), .RR1(ram_1_data[11:9]),
    .RD2(regfile_16bit_x_8_1_rd2), .RR2(ram_1_data[8:6]));  // open: Write, Ck
  Shifter #(.width(16)) shifter_1 (.in(signext_6_to_16bit_1_out), .\dist (4'b0001), .out(shifter_1_out));
  ALU16 alu16_1 (.A(regfile_16bit_x_8_1_rd1), .B(multiplexer_2_out), .F(alu16_1_f));  // open: ALUop
  Multiplexer #(.width(16), .enable("false")) multiplexer_2 (
    .in0(regfile_16bit_x_8_1_rd2), .in1(signext_6_to_16bit_1_out), .out(multiplexer_2_out));  // open: sel
  Multiplexer #(.width(16), .enable("false")) multiplexer_3 (
    .in0(adder_1_out), .in1(adder_2_out), .out(multiplexer_3_out));  // open: sel
  Adder #(.width(16)) adder_2 (.a(adder_1_out), .b(shifter_1_out), .out(adder_2_out));  // open: cin, cout
  RAM #(.addrWidth(16), .dataWidth(16), .bus("separate")) ram_2 (
    .addr(alu16_1_f), .din(regfile_16bit_x_8_1_rd2), .data(ram_2_data));  // open: str, sel, clk, ld, clr
  Multiplexer #(.width(16), .enable("false")) multiplexer_4 (
    .in0(ram_2_data), .in1(alu16_1_f), .out(multiplexer_4_out));  // open: sel

  // Notes on the sheet:
  //   InstMem
  //   DataMem
endmodule

// 6 to 16
module SignExt_6_to_16bit (
  input  [5:0] In,
  output [15:0] Out
);


  assign Out = {{11{In[5]}}, In[4:0]};
endmodule
