// Logisim project 4BitAdder.circ as structural Verilog: 1 circuit, main circuit main
module main (
  input  A4,
  input  B4,
  input  A3,
  input  B3,
  input  A2,
  input  B2,
  input  A1,
  input  B1,
  input  SUB,
  output S4,
  output S3,
  output S2,
  output S1
);

  wire adder_2_cout, adder_3_cout, adder_4_cout, xor_1_out, xor_2_out, xor_3_out, xor_4_out;

  xor xor_1 (xor_1_out, SUB, B4);
  Adder #(.width(1)) adder_1 (.a(xor_1_out), .b(A4), .out(S4), .cin(adder_2_cout));  // open: cout
  xor xor_2 (xor_2_out, SUB, B3);
  Adder #(.width(1)) adder_2 (.a(xor_2_out), .b(A3), .out(S3), .cin(adder_3_cout), .cout(adder_2_cout));
  xor xor_3 (xor_3_out, SUB, B2);
  Adder #(.width(1)) adder_3 (.a(xor_3_out), .b(A2), .out(S2), .cin(adder_4_cout), .cout(adder_3_cout));
  xor xor_4 (xor_4_out, SUB, B1);
  Adder #(.width(1)) adder_4 (.a(xor_4_out), .b(A1), .out(S1), .cin(SUB), .cout(adder_4_cout));

  // Notes on the sheet:
  //   4-Bit Adder/Subtracter
endmodule
