// Logisim project FullAdder.circ as structural Verilog: 1 circuit, main circuit main
module main (
  input  A,
  input  B,
  input  Cin,
  output Cout,
  output S
);

  wire and_1_out, and_2_out, xor_2_out;

  or or_1 (Cout, and_1_out, and_2_out);
  and and_1 (and_1_out, Cin, B);
  and and_2 (and_2_out, A, xor_2_out);
  xor xor_1 (S, A, xor_2_out);
  xor xor_2 (xor_2_out, B, Cin);

  // Notes on the sheet:
  //   Full Adder
endmodule
