// Logisim project GeneralReg.circ as structural Verilog: 1 circuit, main circuit main
module main (
  input  I3,
  input  I2,
  input  I1,
  input  LOAD,
  input  CLEAR,
  output Q3,
  output Q2,
  output Q1
);

  wire and_1_out, and_2_out, and_3_out, and_4_out, and_5_out, and_6_out, CLK_out, not_1_out, not_2_out,
       not_3_out, or_1_out, or_2_out, or_3_out;

  Clock CLK (.out(CLK_out));
  not not_1 (not_1_out, I3);
  and and_1 (and_1_out, LOAD, not_1_out);
  or or_1 (or_1_out, CLEAR, and_1_out);
  and and_2 (and_2_out, LOAD, I3);
  and and_3 (and_3_out, LOAD, not_2_out);
  or or_2 (or_2_out, CLEAR, and_3_out);
  S_R_Flip_Flop s_r_ff_1 (.S(and_2_out), .clk(CLK_out), .R(or_1_out), .Q(Q3));  // open: Qn, preset, reset, en
  not not_2 (not_2_out, I2);
  and and_4 (and_4_out, LOAD, I2);
  or or_3 (or_3_out, CLEAR, and_6_out);
  S_R_Flip_Flop s_r_ff_2 (.S(and_4_out), .clk(CLK_out), .R(or_2_out), .Q(Q2));  // open: Qn, preset, reset, en
  not not_3 (not_3_out, I1);
  and and_5 (and_5_out, LOAD, I1);
  and and_6 (and_6_out, LOAD, not_3_out);
  S_R_Flip_Flop s_r_ff_3 (.S(and_5_out), .clk(CLK_out), .R(or_3_out), .Q(Q1));  // open: Qn, preset, reset, en

  // Notes on the sheet:
  //   3-Bit General-Purpose Register
endmodule
