// Logisim project JKFromSR.circ as structural Verilog: 1 circuit, main circuit main
module main (
  input  J,
  input  K,
  output Q,
  output Q_prime
);

  wire and_1_out, and_2_out, clock_1_out, nand_1_out, nand_2_out;

  Clock clock_1 (.out(clock_1_out));
  nand nand_1 (nand_1_out, Q, K);
  nand nand_2 (nand_2_out, J, Q_prime);
  and and_1 (and_1_out, nand_1_out, J);
  and and_2 (and_2_out, K, nand_2_out);
  S_R_Flip_Flop s_r_ff_1 (
    .S(and_1_out), .clk(clock_1_out), .R(and_2_out), .Q(Q), .Qn(Q_prime));  // open: preset, reset, en

  // Notes on the sheet:
  //   JK Flip Flop
endmodule
