// Logisim project RightShift.circ as structural Verilog: 1 circuit, main circuit main
module main (
  input  Enable,
  input  Fill,
  output Out4,
  output Out3,
  output Out2,
  output Out1
);

  wire and_1_out, and_2_out, and_3_out, and_4_out, and_5_out, and_6_out, and_7_out, and_8_out, CLK_out,
       j_k_ff_1_qn, j_k_ff_2_qn, j_k_ff_3_qn, not_1_out;

  Clock CLK (.out(CLK_out));
  and and_1 (and_1_out, Enable, Fill);
  and and_2 (and_2_out, Enable, not_1_out);
  not not_1 (not_1_out, Fill);
  J_K_Flip_Flop j_k_ff_1 (
    .J(and_1_out), .clk(CLK_out), .K(and_2_out), .Q(Out4), .Qn(j_k_ff_1_qn));  // open: preset, en, reset
  and and_3 (and_3_out, Enable, Out4);
  and and_4 (and_4_out, Enable, j_k_ff_1_qn);
  J_K_Flip_Flop j_k_ff_2 (
    .J(and_3_out), .clk(CLK_out), .K(and_4_out), .Q(Out3), .Qn(j_k_ff_2_qn));  // open: preset, en, reset
  and and_5 (and_5_out, Enable, Out3);
  and and_6 (and_6_out, Enable, j_k_ff_2_qn);
  J_K_Flip_Flop j_k_ff_3 (
    .J(and_5_out), .clk(CLK_out), .K(and_6_out), .Q(Out2), .Qn(j_k_ff_3_qn));  // open: preset, en, reset
  and and_7 (and_7_out, Enable, Out2);
  and and_8 (and_8_out, Enable, j_k_ff_3_qn);
  J_K_Flip_Flop j_k_ff_4 (.J(and_7_out), .clk(CLK_out), .K(and_8_out), .Q(Out1));  // open: Qn, preset, en, reset

  // Notes on the sheet:
  //   Right Shift Register
  //   Change state on PGT of CLK
endmodule
